// Logisim project T64.circ as structural Verilog: 18 circuits, main circuit main
module cpu (
  input  [63:0] Din,
  input  Clock,
  input  Reset,
  output Write,
  output [63:0] Aout,
  output [7:0] Lout,
  output [63:0] Dout
);

  wire alu_1_carryout, alu_1_setcarry, alu_1_zero, AluLoad, and_1_out, and_2_out, and_3_out, and_4_out,
       Carry, ConstLoad, EnPg_q, Jump, MemAddr, MemCycle, not_1_out, PageStructWalk, PDecode, PExec, PFetch1,
       PFetch2, Pointer, RetLoad, SetR, WrReg, Zero;
  wire [1:0] counter_1_q, priority_encoder_1_out;
  wire [3:0] InsLen, RdASel, RdBSel, WrSel;
  wire [7:0] AluOp, Lout_t, mmu_1_lout;
  wire [63:0] adder_2_out, AluOut, Aout_t, bit_extender_1_out, Const, Mask, mmu_1_addrout, multiplexer_1_out,
       multiplexer_3_out, multiplexer_4_out, multiplexer_5_out, multiplexer_6_out, PC, RdAOut, register_2_q,
       register_3_q, RetAddr;

  not not_1 (not_1_out, PageStructWalk);
  Register #(.width(64)) register_1 (.D(multiplexer_1_out), .en(PExec), .Q(PC), .clk(Clock), .clr(Reset));
  Multiplexer #(.enable("false"), .width(64)) multiplexer_1 (
    .in0(RetAddr), .in1(Aout_t), .out(multiplexer_1_out), .sel(Jump));
  Decoder #(.select(2)) decoder_1 (
    .out0(PFetch1), .out1(PFetch2), .out2(PDecode), .out3(PExec), .sel(counter_1_q));  // open: en
  Counter #(.max('h3), .width(2)) counter_1 (
    .count(not_1_out), .Q(counter_1_q), .clk(Clock), .clr(Reset));  // open: load, D, carry, up
  Register #(.width(64)) register_2 (.D(Din), .en(PFetch1), .Q(register_2_q), .clk(Clock), .clr(Reset));
  Register #(.width(64)) register_3 (.D(Din), .en(PFetch2), .Q(register_3_q), .clk(Clock), .clr(Reset));
  assign bit_extender_1_out = {{60{1'b0}}, InsLen};  // Bit_Extender bit_extender_1
  Adder #(.width(64)) adder_1 (.a(PC), .b(bit_extender_1_out), .out(RetAddr));  // open: cin, cout
  Control Control_1 (
    .OpF8(register_2_q), .OpL8(register_3_q), .Clock(Clock), .Reset(Reset), .Exec(PExec), .Carry(Zero),
    .Zero(Carry), .AluOp(AluOp), .ConstOut(Const), .DestReg(WrSel), .Src1(RdASel), .InsLen(InsLen),
    .Src2(RdBSel), .Mask(Mask), .RegWr(WrReg), .Lout(Lout_t), .MemWr(Write), .ConstLoad(ConstLoad),
    .MemAddr(MemAddr), .Pointer(Pointer), .AluLoad(AluLoad), .Jump(Jump), .PCLoad(RetLoad));
  Adder #(.width(64)) adder_2 (.a(PC), .b(64'h8), .out(adder_2_out));  // open: cin, cout
  Priority_Encoder #(.select(2)) priority_encoder_1 (
    .in0(MemAddr), .in1(Pointer), .in2(PFetch2), .in3(PFetch1), .out(priority_encoder_1_out), .gs(MemCycle));  // open: en_out, en_in
  Multiplexer #(.enable("false"), .select(2), .width(64)) multiplexer_2 (
    .in0(Const), .in1(RdAOut), .in2(adder_2_out), .in3(PC), .out(Aout_t), .sel(priority_encoder_1_out));
  Pull_Resistor #(.pull(1)) pull_resistor_1 (.node(priority_encoder_1_out));
  Multiplexer #(.enable("false"), .width(64)) multiplexer_3 (
    .in0(Din), .in1(RetAddr), .out(multiplexer_3_out), .sel(RetLoad));
  Multiplexer #(.enable("false"), .width(64)) multiplexer_4 (
    .in0(multiplexer_3_out), .in1(Const), .out(multiplexer_4_out), .sel(ConstLoad));
  Multiplexer #(.enable("false"), .width(64)) multiplexer_5 (
    .in0(multiplexer_4_out), .in1(AluOut), .out(multiplexer_5_out), .sel(AluLoad));
  and and_1 (and_1_out, AluLoad, ~SetR);  // AND_Gate
  and and_2 (and_2_out, WrReg, ~and_1_out);  // AND_Gate
  D_Flip_Flop EnPg (.Q(EnPg_q));  // open: clk, D, Qn, preset, reset
  regfile regfile_1 (
    .RdBOut(Dout), .RdAOut(RdAOut), .RdBSel(RdBSel), .RdASel(RdASel), .Wrsel(WrSel), .Wr(and_2_out),
    .Reset(Reset), .Mask(Mask), .Din(multiplexer_5_out));
  mmu mmu_1 (
    .AddrIn(Aout_t), .Reset(Reset), .MemCycle(MemCycle), .Clock(Clock), .Din(Din), .AddrOut(mmu_1_addrout),
    .PageStructWalk(PageStructWalk), .Lout(mmu_1_lout));  // open: PL6P_Data, PL6P_Wr, PageFault
  and and_3 (and_3_out, EnPg_q, PageStructWalk);
  Multiplexer #(.enable("false"), .width(64)) multiplexer_6 (
    .in0(Dout), .in1(Const), .out(multiplexer_6_out), .sel(ConstLoad));
  Multiplexer #(.enable("false"), .width(64)) multiplexer_7 (
    .in0(Aout_t), .in1(mmu_1_addrout), .out(Aout), .sel(EnPg_q));
  Multiplexer #(.enable("false"), .width(8)) multiplexer_8 (
    .in0(Lout_t), .in1(mmu_1_lout), .out(Lout), .sel(and_3_out));
  alu alu_1 (
    .A(RdAOut), .B(multiplexer_6_out), .CarryIn(Carry), .Op(AluOp), .Mask(Mask), .R(AluOut),
    .Zero(alu_1_zero), .CarryOut(alu_1_carryout), .SetCarry(alu_1_setcarry), .SetR(SetR));
  D_Flip_Flop d_ff_1 (.clk(Clock), .D(alu_1_zero), .Q(Zero));  // open: Qn, preset, reset
  and and_4 (and_4_out, Clock, alu_1_setcarry);
  D_Flip_Flop d_ff_2 (.clk(and_4_out), .D(alu_1_carryout), .Q(Carry));  // open: Qn, preset, reset

  // Other names for the same wires on the sheet: Clk = Clock; RdBOut[63:0] = Dout
endmodule

module main (
);

  wire and_1_out, button_1_out, clock_1_out, clock_2_out, comparator_1_eq, comparator_2_eq, cpu_1_write;
  wire [7:0] cpu_1_lout;
  wire [63:0] controlled_buffer_1_out, cpu_1_aout, cpu_1_dout, undriven;

  Clock clock_1 (.out(clock_1_out));
  Button button_1 (.out(button_1_out));
  Clock clock_2 (.out(clock_2_out));
  cpu cpu_1 (
    .Din(controlled_buffer_1_out), .Clock(clock_1_out), .Reset(button_1_out), .Write(cpu_1_write),
    .Aout(cpu_1_aout), .Lout(cpu_1_lout), .Dout(cpu_1_dout));
  Comparator #(.width(48)) comparator_1 (.a({48{1'b0}}), .b(cpu_1_aout[63:16]), .eq(comparator_1_eq));  // open: gt, lt
  and and_1 (and_1_out, comparator_1_eq, cpu_1_write);
  Comparator #(.width(40)) comparator_2 (.a({40{1'b1}}), .b(cpu_1_aout[63:24]), .eq(comparator_2_eq));  // open: gt, lt
  // RAM #(.addrWidth(16), .enables("line"), .line("octo"), .misaligned("true")) ram_1: pin names not known; wires that end beside it: cpu_1_aout[15:0], and_1_out, clock_2_out
  assign controlled_buffer_1_out = comparator_1_eq ? undriven : 64'bz;  // Controlled_Buffer controlled_buffer_1
  pciconfhandler pciconfhandler_1 (
    .Dout(controlled_buffer_1_out), .Wr(cpu_1_write), .ConfEn(comparator_2_eq), .Clock(clock_2_out),
    .ConfOffset(cpu_1_aout[7:0]), .DevNoBus(cpu_1_aout[23:8]), .DataIn(cpu_1_dout), .Address(cpu_1_aout));  // open: Bar2, Bar3, Bar4, Bar5, Bar6, Bar7, Bar0, Bar1, NotBAR, DevNo, Bar_LenMask_0, Bar_LenMask_1, Bar_LenMask_2, Bar_LenMask_3, Bar_LenMask_4, Bar_LenMask_5, Bar_LenMask_6, Bar_LenMask_7
endmodule

// RF
module regfile (
  input  [63:0] Mask,
  input  [63:0] Din,
  input  [3:0] RdASel,
  input  Reset,
  input  Wr,
  input  [3:0] RdBSel,
  input  [3:0] Wrsel,
  output [63:0] RdAOut,
  output [63:0] RdBOut
);

  wire demultiplexer_1_out0, demultiplexer_1_out1, demultiplexer_1_out2, demultiplexer_1_out3,
       demultiplexer_1_out4, demultiplexer_1_out5, demultiplexer_1_out6, demultiplexer_1_out7,
       demultiplexer_1_out8, demultiplexer_1_out9, demultiplexer_1_out10, demultiplexer_1_out11,
       demultiplexer_1_out12, demultiplexer_1_out13, demultiplexer_1_out14, demultiplexer_1_out15,
       demultiplexer_1_out16, demultiplexer_1_out17, demultiplexer_1_out18, demultiplexer_1_out19,
       demultiplexer_1_out20, demultiplexer_1_out21, demultiplexer_1_out22, demultiplexer_1_out23,
       demultiplexer_1_out24, demultiplexer_1_out25, demultiplexer_1_out26, demultiplexer_1_out27,
       demultiplexer_1_out28, demultiplexer_1_out29, demultiplexer_1_out30, demultiplexer_1_out31;
  wire [4:0] bit_extender_1_out, bit_extender_2_out, bit_extender_3_out;
  wire [63:0] and_1_out, R0_q, R1_q, R2_q, R3_q, R4_q, R5_q, R6_q, R7_q, R8_q, R9_q, R10_q, R11_q, R12_q,
       R13_q, R14_q, R15_q, register_1_q, register_2_q, register_3_q, register_4_q, register_5_q,
       register_6_q, register_7_q, register_8_q, register_9_q, register_10_q, register_11_q, register_12_q,
       register_13_q, register_14_q, register_15_q, register_16_q;

  Demultiplexer #(.enable("false"), .select(5)) demultiplexer_1 (
    .out0(demultiplexer_1_out0), .out1(demultiplexer_1_out1), .out2(demultiplexer_1_out2),
    .out3(demultiplexer_1_out3), .out4(demultiplexer_1_out4), .out5(demultiplexer_1_out5),
    .out6(demultiplexer_1_out6), .out7(demultiplexer_1_out7), .out8(demultiplexer_1_out8),
    .out9(demultiplexer_1_out9), .out10(demultiplexer_1_out10), .out11(demultiplexer_1_out11),
    .out12(demultiplexer_1_out12), .out13(demultiplexer_1_out13), .out14(demultiplexer_1_out14),
    .out15(demultiplexer_1_out15), .out16(demultiplexer_1_out16), .out17(demultiplexer_1_out17),
    .out18(demultiplexer_1_out18), .out19(demultiplexer_1_out19), .out20(demultiplexer_1_out20),
    .out21(demultiplexer_1_out21), .out22(demultiplexer_1_out22), .out23(demultiplexer_1_out23),
    .out24(demultiplexer_1_out24), .out25(demultiplexer_1_out25), .out26(demultiplexer_1_out26),
    .out27(demultiplexer_1_out27), .out28(demultiplexer_1_out28), .out29(demultiplexer_1_out29),
    .out30(demultiplexer_1_out30), .out31(demultiplexer_1_out31), .in(Wr), .sel(bit_extender_1_out));
  assign bit_extender_1_out = {{1{1'b0}}, Wrsel};  // Bit_Extender bit_extender_1
  assign and_1_out = Mask & Din;  // AND_Gate and_1, 64 bits wide
  Register #(.width(64)) R0 (
    .D(and_1_out), .en(demultiplexer_1_out0), .Q(R0_q), .clk(demultiplexer_1_out0), .clr(Reset));
  Register #(.width(64)) R1 (
    .D(and_1_out), .en(demultiplexer_1_out1), .Q(R1_q), .clk(demultiplexer_1_out1), .clr(Reset));
  Register #(.width(64)) R2 (
    .D(and_1_out), .en(demultiplexer_1_out2), .Q(R2_q), .clk(demultiplexer_1_out2), .clr(Reset));
  Register #(.width(64)) R3 (
    .D(and_1_out), .en(demultiplexer_1_out3), .Q(R3_q), .clk(demultiplexer_1_out3), .clr(Reset));
  Register #(.width(64)) R4 (
    .D(and_1_out), .en(demultiplexer_1_out4), .Q(R4_q), .clk(demultiplexer_1_out4), .clr(Reset));
  Register #(.width(64)) R5 (
    .D(and_1_out), .en(demultiplexer_1_out5), .Q(R5_q), .clk(demultiplexer_1_out5), .clr(Reset));
  Register #(.width(64)) R6 (
    .D(and_1_out), .en(demultiplexer_1_out6), .Q(R6_q), .clk(demultiplexer_1_out6), .clr(Reset));
  Register #(.width(64)) R7 (
    .D(and_1_out), .en(demultiplexer_1_out7), .Q(R7_q), .clk(demultiplexer_1_out7), .clr(Reset));
  Register #(.width(64)) R8 (
    .D(and_1_out), .en(demultiplexer_1_out8), .Q(R8_q), .clk(demultiplexer_1_out8), .clr(Reset));
  Register #(.width(64)) R9 (
    .D(and_1_out), .en(demultiplexer_1_out9), .Q(R9_q), .clk(demultiplexer_1_out9), .clr(Reset));
  Register #(.width(64)) R10 (
    .D(and_1_out), .en(demultiplexer_1_out10), .Q(R10_q), .clk(demultiplexer_1_out10), .clr(Reset));
  Register #(.width(64)) R11 (
    .D(and_1_out), .en(demultiplexer_1_out11), .Q(R11_q), .clk(demultiplexer_1_out11), .clr(Reset));
  Register #(.width(64)) R12 (
    .D(and_1_out), .en(demultiplexer_1_out12), .Q(R12_q), .clk(demultiplexer_1_out12), .clr(Reset));
  Register #(.width(64)) R13 (
    .D(and_1_out), .en(demultiplexer_1_out13), .Q(R13_q), .clk(demultiplexer_1_out13), .clr(Reset));
  Register #(.width(64)) R14 (
    .D(and_1_out), .en(demultiplexer_1_out14), .Q(R14_q), .clk(demultiplexer_1_out14), .clr(Reset));
  Register #(.width(64)) R15 (
    .D(and_1_out), .en(demultiplexer_1_out15), .Q(R15_q), .clk(demultiplexer_1_out15), .clr(Reset));
  Register #(.width(64)) register_1 (
    .D(and_1_out), .en(demultiplexer_1_out16), .Q(register_1_q), .clk(demultiplexer_1_out16), .clr(Reset));
  Register #(.width(64)) register_2 (
    .D(and_1_out), .en(demultiplexer_1_out17), .Q(register_2_q), .clk(demultiplexer_1_out17), .clr(Reset));
  Register #(.width(64)) register_3 (
    .D(and_1_out), .en(demultiplexer_1_out18), .Q(register_3_q), .clk(demultiplexer_1_out18), .clr(Reset));
  Register #(.width(64)) register_4 (
    .D(and_1_out), .en(demultiplexer_1_out19), .Q(register_4_q), .clk(demultiplexer_1_out19), .clr(Reset));
  Register #(.width(64)) register_5 (
    .D(and_1_out), .en(demultiplexer_1_out20), .Q(register_5_q), .clk(demultiplexer_1_out20), .clr(Reset));
  Register #(.width(64)) register_6 (
    .D(and_1_out), .en(demultiplexer_1_out21), .Q(register_6_q), .clk(demultiplexer_1_out21), .clr(Reset));
  Register #(.width(64)) register_7 (
    .D(and_1_out), .en(demultiplexer_1_out22), .Q(register_7_q), .clk(demultiplexer_1_out22), .clr(Reset));
  Register #(.width(64)) register_8 (
    .D(and_1_out), .en(demultiplexer_1_out23), .Q(register_8_q), .clk(demultiplexer_1_out23), .clr(Reset));
  Register #(.width(64)) register_9 (
    .D(and_1_out), .en(demultiplexer_1_out24), .Q(register_9_q), .clk(demultiplexer_1_out24), .clr(Reset));
  Register #(.width(64)) register_10 (
    .D(and_1_out), .en(demultiplexer_1_out25), .Q(register_10_q), .clk(demultiplexer_1_out25), .clr(Reset));
  Register #(.width(64)) register_11 (
    .D(and_1_out), .en(demultiplexer_1_out26), .Q(register_11_q), .clk(demultiplexer_1_out26), .clr(Reset));
  Register #(.width(64)) register_12 (
    .D(and_1_out), .en(demultiplexer_1_out27), .Q(register_12_q), .clk(demultiplexer_1_out27), .clr(Reset));
  Register #(.width(64)) register_13 (
    .D(and_1_out), .en(demultiplexer_1_out28), .Q(register_13_q), .clk(demultiplexer_1_out28), .clr(Reset));
  Register #(.width(64)) register_14 (
    .D(and_1_out), .en(demultiplexer_1_out29), .Q(register_14_q), .clk(demultiplexer_1_out29), .clr(Reset));
  Register #(.width(64)) register_15 (
    .D(and_1_out), .en(demultiplexer_1_out30), .Q(register_15_q), .clk(demultiplexer_1_out30), .clr(Reset));
  Register #(.width(64)) register_16 (
    .D(and_1_out), .en(demultiplexer_1_out31), .Q(register_16_q), .clk(demultiplexer_1_out31), .clr(Reset));
  Multiplexer #(.enable("false"), .select(5), .width(64)) multiplexer_1 (
    .in0(R0_q), .in1(R1_q), .in2(R2_q), .in3(R3_q), .in4(R4_q), .in5(R5_q), .in6(R6_q), .in7(R7_q),
    .in8(R8_q), .in9(R9_q), .in10(R10_q), .in11(R11_q), .in12(R12_q), .in13(R13_q), .in14(R14_q),
    .in15(R15_q), .in16(register_1_q), .in17(register_2_q), .in18(register_3_q), .in19(register_4_q),
    .in20(register_5_q), .in21(register_6_q), .in22(register_7_q), .in23(register_8_q), .in24(register_9_q),
    .in25(register_10_q), .in26(register_11_q), .in27(register_12_q), .in28(register_13_q),
    .in29(register_14_q), .in30(register_15_q), .in31(register_16_q), .out(RdAOut), .sel(bit_extender_2_out));
  Multiplexer #(.enable("false"), .select(5), .width(64)) multiplexer_2 (
    .in0(R0_q), .in1(R1_q), .in2(R2_q), .in3(R3_q), .in4(R4_q), .in5(R5_q), .in6(R6_q), .in7(R7_q),
    .in8(R8_q), .in9(R9_q), .in10(R10_q), .in11(R11_q), .in12(R12_q), .in13(R13_q), .in14(R14_q),
    .in15(R15_q), .in16(register_1_q), .in17(register_2_q), .in18(register_3_q), .in19(register_4_q),
    .in20(register_5_q), .in21(register_6_q), .in22(register_7_q), .in23(register_8_q), .in24(register_9_q),
    .in25(register_10_q), .in26(register_11_q), .in27(register_12_q), .in28(register_13_q),
    .in29(register_14_q), .in30(register_15_q), .in31(register_16_q), .out(RdBOut), .sel(bit_extender_3_out));
  assign bit_extender_2_out = {{1{1'b0}}, RdASel};  // Bit_Extender bit_extender_2
  assign bit_extender_3_out = {{1{1'b0}}, RdBSel};  // Bit_Extender bit_extender_3
endmodule

module Control (
  input  [63:0] OpF8,
  input  [63:0] OpL8,
  input  Clock,
  input  Reset,
  input  Exec,
  input  Carry,
  input  Zero,
  output [7:0] AluOp,
  output [63:0] ConstOut,
  output [3:0] DestReg,
  output [3:0] Src1,
  output [3:0] InsLen,
  output [3:0] Src2,
  output [63:0] Mask,
  output RegWr,
  output [7:0] Lout,
  output MemWr,
  output ConstLoad,
  output MemAddr,
  output Pointer,
  output AluLoad,
  output Jump,
  output PCLoad
);

  wire and_1_out, and_2_out, and_3_out, and_4_out, and_7_out, and_9_out, comparator_1_eq, comparator_2_eq,
       comparator_3_eq, comparator_4_eq, comparator_6_eq, comparator_7_eq, decoder_1_out0, decoder_1_out8,
       or_2_out, or_3_out, rom_2_data, rom_3_data, rom_5_data;
  wire [3:0] adder_1_out, rom_1_data, rom_6_data;

  Decoder #(.select(4)) decoder_1 (
    .out0(decoder_1_out0), .out1(MemAddr), .out2(Pointer), .out8(decoder_1_out8), .sel(OpF8[15:12]));  // open: out3, out4, out5, out6, out7, out9, out10, out11, out12, out13, out14, out15, en
  or or_1 (ConstLoad, decoder_1_out0, decoder_1_out8);
  ROM #(.dataWidth(4)) rom_1 (.addr(OpF8[7:0]), .data(rom_1_data));
  ROM #(.dataWidth(1)) rom_2 (.addr(OpF8[7:0]), .data(rom_2_data));
  ROM #(.dataWidth(1)) rom_3 (.addr(OpF8[7:0]), .data(rom_3_data));
  ROM #(.dataWidth(1)) rom_4 (.addr(OpF8[7:0]), .data(AluLoad));
  ROM #(.dataWidth(1)) rom_5 (.addr(OpF8[7:0]), .data(rom_5_data));
  ROM #(.addrWidth(4), .dataWidth(4)) rom_6 (.addr(OpF8[15:12]), .data(rom_6_data));
  Comparator #(.mode("unsigned")) comparator_1 (.a(OpF8[7:0]), .b(8'hd), .eq(comparator_1_eq));  // open: gt, lt
  Comparator #(.mode("unsigned")) comparator_2 (.a(OpF8[7:0]), .b(8'he), .eq(comparator_2_eq));  // open: gt, lt
  Comparator #(.mode("unsigned")) comparator_3 (.a(OpF8[7:0]), .b(8'hf), .eq(comparator_3_eq));  // open: gt, lt
  Comparator #(.mode("unsigned")) comparator_4 (.a(OpF8[7:0]), .b(8'h10), .eq(comparator_4_eq));  // open: gt, lt
  Comparator #(.mode("unsigned")) comparator_5 (.a(OpF8[7:0]), .b(8'h11), .eq(PCLoad));  // open: gt, lt
  Multiplexer #(.enable("false"), .width(64)) multiplexer_1 (
    .in0({OpL8[23:0], OpF8[63:24]}), .in1({OpL8[31:0], OpF8[63:32]}), .out(ConstOut), .sel(comparator_6_eq));
  and and_1 (and_1_out, comparator_1_eq, ~Zero);  // AND_Gate
  and and_2 (and_2_out, comparator_2_eq, Zero);
  and and_3 (and_3_out, comparator_3_eq, ~Carry);  // AND_Gate
  and and_4 (and_4_out, comparator_4_eq, Carry);
  and and_5 (RegWr, Exec, rom_2_data);
  and and_6 (MemWr, Exec, rom_3_data);
  and and_7 (and_7_out, Exec, rom_5_data);
  or or_2 (or_2_out, and_1_out, and_2_out, and_3_out, and_4_out);
  and and_8 (Jump, and_7_out, ~or_2_out);  // AND_Gate
  Comparator #(.width(4)) comparator_6 (.a(4'b1000), .b(OpF8[15:12]), .eq(comparator_6_eq));  // open: gt, lt
  ROM #(.addrWidth(4), .dataWidth(64)) rom_7 (.addr(rom_1_data), .data(Mask));
  ROM #(.addrWidth(4)) rom_8 (.addr(rom_1_data), .data(Lout));
  and and_9 (and_9_out, ~OpF8[31], comparator_6_eq);  // AND_Gate
  Comparator #(.width(4)) comparator_7 (.a(OpF8[15:12]), .b(4'b0000), .eq(comparator_7_eq));  // open: gt, lt
  Adder #(.width(4)) adder_1 (.a(rom_1_data), .b(rom_6_data), .out(adder_1_out));  // open: cin, cout
  or or_3 (or_3_out, and_9_out, comparator_7_eq);
  Multiplexer #(.enable("false"), .width(4)) multiplexer_2 (
    .in0(rom_6_data), .in1(adder_1_out), .out(InsLen), .sel(or_3_out));

  assign AluOp = OpF8[31:24];
  assign DestReg = OpF8[11:8];
  assign Src1 = OpF8[23:20];
  assign Src2 = OpF8[19:16];

  // Notes on the sheet:
  //   contents of rom_1 (hex, n*v repeats v):
  //   1 2 4 8 1 2 4 8 1 2 4 8
  //   contents of rom_2 (hex, n*v repeats v):
  //   4*1 4*0 4*1 5*0 1
  //   contents of rom_3 (hex, n*v repeats v):
  //   4*0 4*1
  //   contents of rom_4 (hex, n*v repeats v):
  //   8*0 4*1
  //   contents of rom_5 (hex, n*v repeats v):
  //   12*0 6*1
  //   contents of rom_6 (hex, n*v repeats v):
  //   3 b 3 4*0 4 4
  //   contents of rom_7 (hex, n*v repeats v):
  //   0 ff ffff ffffff
  //   contents of rom_8 (hex, n*v repeats v):
  //   0 1 3 7 f 1f 3f 7f ff
endmodule

module alu (
  input  [63:0] A,
  input  [63:0] B,
  input  CarryIn,
  input  [7:0] Op,
  input  [63:0] Mask,
  output [63:0] R,
  output Zero,
  output CarryOut,
  output SetCarry,
  output SetR
);

  wire alu8_1_carryout, alu8_1_setcarry, alu8_1_setr, alu8_1_zero, alu16_1_carryout, alu16_1_setcarry,
       alu16_1_setr, alu16_1_zero, alu32_1_carryout, alu32_1_setcarry, alu32_1_setr, alu32_1_zero,
       alu64_1_carryout, alu64_1_setcarry, alu64_1_setr, alu64_1_zero, comparator_1_eq, comparator_2_eq,
       comparator_3_eq, comparator_4_eq;
  wire [1:0] priority_encoder_1_out;
  wire [63:0] alu8_1_r, alu16_1_r, alu32_1_r, alu64_1_r;

  Comparator #(.width(64)) comparator_1 (.a(Mask), .b(64'hff), .eq(comparator_1_eq));  // open: gt, lt
  Comparator #(.width(64)) comparator_2 (.a(Mask), .b(64'hffff), .eq(comparator_2_eq));  // open: gt, lt
  Comparator #(.width(64)) comparator_3 (.a(Mask), .b(64'hffffffff), .eq(comparator_3_eq));  // open: gt, lt
  Comparator #(.width(64)) comparator_4 (.a(Mask), .b({64{1'b1}}), .eq(comparator_4_eq));  // open: gt, lt
  alu8 alu8_1 (
    .A(A), .B(B), .CarryIn(CarryIn), .Op(Op), .R(alu8_1_r), .Zero(alu8_1_zero), .CarryOut(alu8_1_carryout),
    .SetCarry(alu8_1_setcarry), .SetR(alu8_1_setr));
  alu16 alu16_1 (
    .A(A), .B(B), .CarryIn(CarryIn), .Op(Op), .R(alu16_1_r), .Zero(alu16_1_zero),
    .CarryOut(alu16_1_carryout), .SetCarry(alu16_1_setcarry), .SetR(alu16_1_setr));
  alu32 alu32_1 (
    .A(A), .B(B), .CarryIn(CarryIn), .Op(Op), .R(alu32_1_r), .Zero(alu32_1_zero),
    .CarryOut(alu32_1_carryout), .SetCarry(alu32_1_setcarry), .SetR(alu32_1_setr));
  alu64 alu64_1 (
    .A(A), .B(B), .CarryIn(CarryIn), .Op(Op), .R(alu64_1_r), .Zero(alu64_1_zero),
    .CarryOut(alu64_1_carryout), .SetCarry(alu64_1_setcarry), .SetR(alu64_1_setr));
  Priority_Encoder #(.select(2)) priority_encoder_1 (
    .in0(comparator_1_eq), .in1(comparator_2_eq), .in2(comparator_3_eq), .in3(comparator_4_eq),
    .out(priority_encoder_1_out));  // open: gs, en_out, en_in
  Pull_Resistor pull_resistor_1 (.node(priority_encoder_1_out));
  Multiplexer #(.enable("false"), .select(2), .width(64)) multiplexer_1 (
    .in0(alu8_1_r), .in1(alu16_1_r), .in2(alu32_1_r), .in3(alu64_1_r), .out(R), .sel(priority_encoder_1_out));
  Multiplexer #(.enable("false"), .select(2)) multiplexer_2 (
    .in0(alu8_1_zero), .in1(alu16_1_zero), .in2(alu32_1_zero), .in3(alu64_1_zero), .out(Zero),
    .sel(priority_encoder_1_out));
  Multiplexer #(.enable("false"), .select(2)) multiplexer_3 (
    .in0(alu8_1_carryout), .in1(alu16_1_carryout), .in2(alu32_1_carryout), .in3(alu64_1_carryout),
    .out(CarryOut), .sel(priority_encoder_1_out));
  Multiplexer #(.enable("false"), .select(2)) multiplexer_4 (
    .in0(alu8_1_setcarry), .in1(alu16_1_setcarry), .in2(alu32_1_setcarry), .in3(alu64_1_setcarry),
    .out(SetCarry), .sel(priority_encoder_1_out));
  Multiplexer #(.enable("false"), .select(2)) multiplexer_5 (
    .in0(alu8_1_setr), .in1(alu16_1_setr), .in2(alu32_1_setr), .in3(alu64_1_setr), .out(SetR),
    .sel(priority_encoder_1_out));
endmodule

module alu8 (
  input  [63:0] A,
  input  [63:0] B,
  input  CarryIn,
  input  [7:0] Op,
  output [63:0] R,
  output Zero,
  output CarryOut,
  output SetCarry,
  output SetR
);

  wire adder_1_cout, and_1_out, and_2_out, controlled_buffer_5_out, decoder_1_out0, decoder_1_out1,
       decoder_1_out2, decoder_1_out3, decoder_1_out4, decoder_1_out5, decoder_1_out6, decoder_1_out7,
       decoder_1_out8, decoder_1_out9, decoder_1_out10, decoder_1_out11, decoder_1_out12, decoder_1_out13,
       decoder_1_out14, decoder_1_out15, decoder_1_out16, or_1_out, or_2_out, subtractor_1_bout;
  wire [7:0] adder_1_out, and_3_out, bit_extender_1_out, bit_extender_2_out, controlled_buffer_1_out,
       divider_1_out, divider_1_rem, divider_2_out, divider_2_rem, multiplier_1_cout, multiplier_1_out,
       multiplier_2_cout, multiplier_2_out, negator_1_out, not_1_out, or_3_out, subtractor_1_out;
  wire [63:0] multiplexer_1_out;

  Decoder #(.select(5)) decoder_1 (
    .out0(decoder_1_out0), .out1(decoder_1_out1), .out2(decoder_1_out2), .out3(decoder_1_out3),
    .out4(decoder_1_out4), .out5(decoder_1_out5), .out6(decoder_1_out6), .out7(decoder_1_out7),
    .out8(decoder_1_out8), .out9(decoder_1_out9), .out10(decoder_1_out10), .out11(decoder_1_out11),
    .out12(decoder_1_out12), .out13(decoder_1_out13), .out14(decoder_1_out14), .out15(decoder_1_out15),
    .out16(decoder_1_out16), .sel(Op[4:0]));  // open: out17, out18, out19, out20, out21, out22, out23, out24, out25, out26, out27, out28, out29, out30, out31, en
  Multiplexer #(.enable("false"), .width(64)) multiplexer_1 (
    .in0(B), .in1({64{1'b0}}), .out(multiplexer_1_out), .sel(Op[7]));
  and and_1 (and_1_out, decoder_1_out14, CarryIn);
  and and_2 (and_2_out, decoder_1_out15, CarryIn);
  Bit_Extender #(.in_width(64), .out_width(8), .\type ("zero")) bit_extender_1 (.in(A), .out(bit_extender_1_out));
  Bit_Extender #(.in_width(64), .out_width(8), .\type ("zero")) bit_extender_2 (
    .in(multiplexer_1_out), .out(bit_extender_2_out));
  or or_1 (or_1_out, decoder_1_out14, decoder_1_out16, decoder_1_out3);
  or or_2 (or_2_out, decoder_1_out15, decoder_1_out4);
  assign not_1_out = ~bit_extender_1_out;  // NOT_Gate not_1, 8 bits wide
  assign and_3_out = bit_extender_1_out & bit_extender_2_out;  // AND_Gate and_3, 8 bits wide
  assign or_3_out = bit_extender_1_out | bit_extender_2_out;  // OR_Gate or_3, 8 bits wide
  Adder adder_1 (
    .a(bit_extender_1_out), .b(bit_extender_2_out), .out(adder_1_out), .cin(and_1_out), .cout(adder_1_cout));
  Subtractor subtractor_1 (
    .a(bit_extender_1_out), .b(bit_extender_2_out), .out(subtractor_1_out), .bin(and_2_out),
    .bout(subtractor_1_bout));
  Multiplier multiplier_1 (
    .a(bit_extender_1_out), .b(bit_extender_2_out), .out(multiplier_1_out), .cout(multiplier_1_cout));  // open: cin
  Multiplier #(.mode("twosComplement")) multiplier_2 (
    .a(bit_extender_1_out), .b(bit_extender_2_out), .out(multiplier_2_out), .cout(multiplier_2_cout));  // open: cin
  Divider divider_1 (
    .a(bit_extender_1_out), .b(bit_extender_2_out), .out(divider_1_out), .rem(divider_1_rem));  // open: upper
  Divider #(.mode("twosComplement")) divider_2 (
    .a(bit_extender_1_out), .b(bit_extender_2_out), .out(divider_2_out), .rem(divider_2_rem));  // open: upper
  Negator negator_1 (.in(bit_extender_1_out), .out(negator_1_out));
  not not_2 (SetR, decoder_1_out16);
  assign R = {{56{1'b0}}, controlled_buffer_1_out};  // Bit_Extender bit_extender_3
  assign controlled_buffer_1_out = decoder_1_out0 ? not_1_out : 8'bz;  // Controlled_Buffer controlled_buffer_1
  assign controlled_buffer_1_out = decoder_1_out1 ? and_3_out : 8'bz;  // Controlled_Buffer controlled_buffer_2
  assign controlled_buffer_1_out = decoder_1_out2 ? or_3_out : 8'bz;  // Controlled_Buffer controlled_buffer_3
  Pull_Resistor pull_resistor_1 (.node(controlled_buffer_1_out));
  assign controlled_buffer_1_out = or_1_out ? adder_1_out : 8'bz;  // Controlled_Buffer controlled_buffer_4
  assign controlled_buffer_5_out = or_1_out ? adder_1_cout : 1'bz;  // Controlled_Buffer controlled_buffer_5
  assign controlled_buffer_1_out = or_2_out ? subtractor_1_out : 8'bz;  // Controlled_Buffer controlled_buffer_6
  assign controlled_buffer_5_out = or_2_out ? subtractor_1_bout : 1'bz;  // Controlled_Buffer controlled_buffer_7
  assign controlled_buffer_1_out = decoder_1_out5 ? multiplier_1_out : 8'bz;  // Controlled_Buffer controlled_buffer_8
  assign controlled_buffer_1_out = decoder_1_out6 ? multiplier_1_cout : 8'bz;  // Controlled_Buffer controlled_buffer_9
  assign controlled_buffer_1_out = decoder_1_out7 ? multiplier_2_out : 8'bz;  // Controlled_Buffer controlled_buffer_10
  assign controlled_buffer_1_out = decoder_1_out8 ? multiplier_2_cout : 8'bz;  // Controlled_Buffer controlled_buffer_11
  assign controlled_buffer_1_out = decoder_1_out9 ? divider_1_out : 8'bz;  // Controlled_Buffer controlled_buffer_12
  assign controlled_buffer_1_out = decoder_1_out10 ? divider_1_rem : 8'bz;  // Controlled_Buffer controlled_buffer_13
  assign controlled_buffer_1_out = decoder_1_out11 ? divider_2_out : 8'bz;  // Controlled_Buffer controlled_buffer_14
  assign controlled_buffer_1_out = decoder_1_out12 ? divider_2_rem : 8'bz;  // Controlled_Buffer controlled_buffer_15
  assign controlled_buffer_1_out = decoder_1_out13 ? negator_1_out : 8'bz;  // Controlled_Buffer controlled_buffer_16
  Pull_Resistor pull_resistor_2 (.node(controlled_buffer_5_out));
  or or_4 (SetCarry, or_1_out, or_2_out);
  Comparator #(.mode("unsigned")) comparator_1 (.a(controlled_buffer_1_out), .b({8{1'b0}}), .eq(Zero));  // open: gt, lt
  and and_4 (CarryOut, controlled_buffer_5_out, SetCarry);
endmodule

module alu16 (
  input  [63:0] A,
  input  [63:0] B,
  input  CarryIn,
  input  [7:0] Op,
  output [63:0] R,
  output Zero,
  output CarryOut,
  output SetCarry,
  output SetR
);

  wire adder_1_cout, and_1_out, and_2_out, controlled_buffer_15_out, decoder_1_out0, decoder_1_out1,
       decoder_1_out2, decoder_1_out3, decoder_1_out4, decoder_1_out5, decoder_1_out6, decoder_1_out7,
       decoder_1_out8, decoder_1_out9, decoder_1_out10, decoder_1_out11, decoder_1_out12, decoder_1_out13,
       decoder_1_out14, decoder_1_out15, decoder_1_out16, or_1_out, or_2_out, subtractor_1_bout;
  wire [15:0] adder_1_out, and_3_out, bit_extender_1_out, bit_extender_2_out, controlled_buffer_1_out,
       divider_1_out, divider_1_rem, divider_2_out, divider_2_rem, multiplier_1_cout, multiplier_1_out,
       multiplier_2_cout, multiplier_2_out, negator_1_out, not_1_out, or_3_out, subtractor_1_out;
  wire [63:0] multiplexer_1_out;

  Multiplexer #(.enable("false"), .width(64)) multiplexer_1 (
    .in0(B), .in1({64{1'b0}}), .out(multiplexer_1_out), .sel(Op[7]));
  Decoder #(.select(5)) decoder_1 (
    .out0(decoder_1_out0), .out1(decoder_1_out1), .out2(decoder_1_out2), .out3(decoder_1_out3),
    .out4(decoder_1_out4), .out5(decoder_1_out5), .out6(decoder_1_out6), .out7(decoder_1_out7),
    .out8(decoder_1_out8), .out9(decoder_1_out9), .out10(decoder_1_out10), .out11(decoder_1_out11),
    .out12(decoder_1_out12), .out13(decoder_1_out13), .out14(decoder_1_out14), .out15(decoder_1_out15),
    .out16(decoder_1_out16), .sel(Op[4:0]));  // open: out17, out18, out19, out20, out21, out22, out23, out24, out25, out26, out27, out28, out29, out30, out31, en
  and and_1 (and_1_out, decoder_1_out14, CarryIn);
  and and_2 (and_2_out, decoder_1_out15, CarryIn);
  Bit_Extender #(.in_width(64), .\type ("zero")) bit_extender_1 (.in(A), .out(bit_extender_1_out));
  Bit_Extender #(.in_width(64), .\type ("zero")) bit_extender_2 (.in(multiplexer_1_out), .out(bit_extender_2_out));
  or or_1 (or_1_out, decoder_1_out14, decoder_1_out16, decoder_1_out3);
  or or_2 (or_2_out, decoder_1_out15, decoder_1_out4);
  assign not_1_out = ~bit_extender_1_out;  // NOT_Gate not_1, 16 bits wide
  assign controlled_buffer_1_out = decoder_1_out0 ? not_1_out : 16'bz;  // Controlled_Buffer controlled_buffer_1
  assign and_3_out = bit_extender_1_out & bit_extender_2_out;  // AND_Gate and_3, 16 bits wide
  assign controlled_buffer_1_out = decoder_1_out1 ? and_3_out : 16'bz;  // Controlled_Buffer controlled_buffer_2
  assign or_3_out = bit_extender_1_out | bit_extender_2_out;  // OR_Gate or_3, 16 bits wide
  assign controlled_buffer_1_out = decoder_1_out2 ? or_3_out : 16'bz;  // Controlled_Buffer controlled_buffer_3
  assign controlled_buffer_1_out = or_1_out ? adder_1_out : 16'bz;  // Controlled_Buffer controlled_buffer_4
  Adder #(.width(16)) adder_1 (
    .a(bit_extender_1_out), .b(bit_extender_2_out), .out(adder_1_out), .cin(and_1_out), .cout(adder_1_cout));
  assign controlled_buffer_1_out = or_2_out ? subtractor_1_out : 16'bz;  // Controlled_Buffer controlled_buffer_5
  Subtractor #(.width(16)) subtractor_1 (
    .a(bit_extender_1_out), .b(bit_extender_2_out), .out(subtractor_1_out), .bin(and_2_out),
    .bout(subtractor_1_bout));
  assign controlled_buffer_1_out = decoder_1_out5 ? multiplier_1_out : 16'bz;  // Controlled_Buffer controlled_buffer_6
  Multiplier #(.width(16)) multiplier_1 (
    .a(bit_extender_1_out), .b(bit_extender_2_out), .out(multiplier_1_out), .cout(multiplier_1_cout));  // open: cin
  assign controlled_buffer_1_out = decoder_1_out6 ? multiplier_1_cout : 16'bz;  // Controlled_Buffer controlled_buffer_7
  assign controlled_buffer_1_out = decoder_1_out7 ? multiplier_2_out : 16'bz;  // Controlled_Buffer controlled_buffer_8
  Multiplier #(.mode("twosComplement"), .width(16)) multiplier_2 (
    .a(bit_extender_1_out), .b(bit_extender_2_out), .out(multiplier_2_out), .cout(multiplier_2_cout));  // open: cin
  assign controlled_buffer_1_out = decoder_1_out8 ? multiplier_2_cout : 16'bz;  // Controlled_Buffer controlled_buffer_9
  assign controlled_buffer_1_out = decoder_1_out9 ? divider_1_out : 16'bz;  // Controlled_Buffer controlled_buffer_10
  Divider #(.width(16)) divider_1 (
    .a(bit_extender_1_out), .b(bit_extender_2_out), .out(divider_1_out), .rem(divider_1_rem));  // open: upper
  assign controlled_buffer_1_out = decoder_1_out10 ? divider_1_rem : 16'bz;  // Controlled_Buffer controlled_buffer_11
  assign controlled_buffer_1_out = decoder_1_out11 ? divider_2_out : 16'bz;  // Controlled_Buffer controlled_buffer_12
  Divider #(.mode("twosComplement"), .width(16)) divider_2 (
    .a(bit_extender_1_out), .b(bit_extender_2_out), .out(divider_2_out), .rem(divider_2_rem));  // open: upper
  assign controlled_buffer_1_out = decoder_1_out12 ? divider_2_rem : 16'bz;  // Controlled_Buffer controlled_buffer_13
  assign controlled_buffer_1_out = decoder_1_out13 ? negator_1_out : 16'bz;  // Controlled_Buffer controlled_buffer_14
  Negator #(.width(16)) negator_1 (.in(bit_extender_1_out), .out(negator_1_out));
  not not_2 (SetR, decoder_1_out16);
  assign R = {{48{1'b0}}, controlled_buffer_1_out};  // Bit_Extender bit_extender_3
  Pull_Resistor pull_resistor_1 (.node(controlled_buffer_1_out));
  assign controlled_buffer_15_out = or_1_out ? adder_1_cout : 1'bz;  // Controlled_Buffer controlled_buffer_15
  assign controlled_buffer_15_out = or_2_out ? subtractor_1_bout : 1'bz;  // Controlled_Buffer controlled_buffer_16
  Pull_Resistor pull_resistor_2 (.node(controlled_buffer_15_out));
  or or_4 (SetCarry, or_1_out, or_2_out);
  Comparator #(.mode("unsigned"), .width(16)) comparator_1 (
    .a(controlled_buffer_1_out), .b({16{1'b0}}), .eq(Zero));  // open: gt, lt
  and and_4 (CarryOut, controlled_buffer_15_out, SetCarry);
endmodule

module alu32 (
  input  [63:0] A,
  input  [63:0] B,
  input  CarryIn,
  input  [7:0] Op,
  output [63:0] R,
  output Zero,
  output CarryOut,
  output SetCarry,
  output SetR
);

  wire adder_1_cout, and_1_out, and_2_out, controlled_buffer_15_out, decoder_1_out0, decoder_1_out1,
       decoder_1_out2, decoder_1_out3, decoder_1_out4, decoder_1_out5, decoder_1_out6, decoder_1_out7,
       decoder_1_out8, decoder_1_out9, decoder_1_out10, decoder_1_out11, decoder_1_out12, decoder_1_out13,
       decoder_1_out14, decoder_1_out15, decoder_1_out16, or_1_out, or_2_out, subtractor_1_bout;
  wire [31:0] adder_1_out, and_3_out, bit_extender_1_out, bit_extender_2_out, controlled_buffer_1_out,
       divider_1_out, divider_1_rem, divider_2_out, divider_2_rem, multiplier_1_cout, multiplier_1_out,
       multiplier_2_cout, multiplier_2_out, negator_1_out, not_1_out, or_3_out, subtractor_1_out;
  wire [63:0] multiplexer_1_out;

  Multiplexer #(.enable("false"), .width(64)) multiplexer_1 (
    .in0(B), .in1({64{1'b0}}), .out(multiplexer_1_out), .sel(Op[7]));
  Decoder #(.select(5)) decoder_1 (
    .out0(decoder_1_out0), .out1(decoder_1_out1), .out2(decoder_1_out2), .out3(decoder_1_out3),
    .out4(decoder_1_out4), .out5(decoder_1_out5), .out6(decoder_1_out6), .out7(decoder_1_out7),
    .out8(decoder_1_out8), .out9(decoder_1_out9), .out10(decoder_1_out10), .out11(decoder_1_out11),
    .out12(decoder_1_out12), .out13(decoder_1_out13), .out14(decoder_1_out14), .out15(decoder_1_out15),
    .out16(decoder_1_out16), .sel(Op[4:0]));  // open: out17, out18, out19, out20, out21, out22, out23, out24, out25, out26, out27, out28, out29, out30, out31, en
  Bit_Extender #(.in_width(64), .out_width(32), .\type ("zero")) bit_extender_1 (.in(A), .out(bit_extender_1_out));
  Bit_Extender #(.in_width(64), .out_width(32), .\type ("zero")) bit_extender_2 (
    .in(multiplexer_1_out), .out(bit_extender_2_out));
  and and_1 (and_1_out, decoder_1_out14, CarryIn);
  and and_2 (and_2_out, decoder_1_out15, CarryIn);
  or or_1 (or_1_out, decoder_1_out14, decoder_1_out16, decoder_1_out3);
  or or_2 (or_2_out, decoder_1_out15, decoder_1_out4);
  assign not_1_out = ~bit_extender_1_out;  // NOT_Gate not_1, 32 bits wide
  assign controlled_buffer_1_out = decoder_1_out0 ? not_1_out : 32'bz;  // Controlled_Buffer controlled_buffer_1
  assign and_3_out = bit_extender_1_out & bit_extender_2_out;  // AND_Gate and_3, 32 bits wide
  assign controlled_buffer_1_out = decoder_1_out1 ? and_3_out : 32'bz;  // Controlled_Buffer controlled_buffer_2
  assign or_3_out = bit_extender_1_out | bit_extender_2_out;  // OR_Gate or_3, 32 bits wide
  assign controlled_buffer_1_out = decoder_1_out2 ? or_3_out : 32'bz;  // Controlled_Buffer controlled_buffer_3
  assign controlled_buffer_1_out = or_1_out ? adder_1_out : 32'bz;  // Controlled_Buffer controlled_buffer_4
  Adder #(.width(32)) adder_1 (
    .a(bit_extender_1_out), .b(bit_extender_2_out), .out(adder_1_out), .cin(and_1_out), .cout(adder_1_cout));
  assign controlled_buffer_1_out = or_2_out ? subtractor_1_out : 32'bz;  // Controlled_Buffer controlled_buffer_5
  Subtractor #(.width(32)) subtractor_1 (
    .a(bit_extender_1_out), .b(bit_extender_2_out), .out(subtractor_1_out), .bin(and_2_out),
    .bout(subtractor_1_bout));
  assign controlled_buffer_1_out = decoder_1_out5 ? multiplier_1_out : 32'bz;  // Controlled_Buffer controlled_buffer_6
  Multiplier #(.width(32)) multiplier_1 (
    .a(bit_extender_1_out), .b(bit_extender_2_out), .out(multiplier_1_out), .cout(multiplier_1_cout));  // open: cin
  assign controlled_buffer_1_out = decoder_1_out6 ? multiplier_1_cout : 32'bz;  // Controlled_Buffer controlled_buffer_7
  assign controlled_buffer_1_out = decoder_1_out7 ? multiplier_2_out : 32'bz;  // Controlled_Buffer controlled_buffer_8
  Multiplier #(.mode("twosComplement"), .width(32)) multiplier_2 (
    .a(bit_extender_1_out), .b(bit_extender_2_out), .out(multiplier_2_out), .cout(multiplier_2_cout));  // open: cin
  assign controlled_buffer_1_out = decoder_1_out8 ? multiplier_2_cout : 32'bz;  // Controlled_Buffer controlled_buffer_9
  assign controlled_buffer_1_out = decoder_1_out9 ? divider_1_out : 32'bz;  // Controlled_Buffer controlled_buffer_10
  Divider #(.width(32)) divider_1 (
    .a(bit_extender_1_out), .b(bit_extender_2_out), .out(divider_1_out), .rem(divider_1_rem));  // open: upper
  assign controlled_buffer_1_out = decoder_1_out10 ? divider_1_rem : 32'bz;  // Controlled_Buffer controlled_buffer_11
  assign controlled_buffer_1_out = decoder_1_out11 ? divider_2_out : 32'bz;  // Controlled_Buffer controlled_buffer_12
  Divider #(.mode("twosComplement"), .width(32)) divider_2 (
    .a(bit_extender_1_out), .b(bit_extender_2_out), .out(divider_2_out), .rem(divider_2_rem));  // open: upper
  assign controlled_buffer_1_out = decoder_1_out12 ? divider_2_rem : 32'bz;  // Controlled_Buffer controlled_buffer_13
  assign controlled_buffer_1_out = decoder_1_out13 ? negator_1_out : 32'bz;  // Controlled_Buffer controlled_buffer_14
  Negator #(.width(32)) negator_1 (.in(bit_extender_1_out), .out(negator_1_out));
  not not_2 (SetR, decoder_1_out16);
  assign R = {{32{1'b0}}, controlled_buffer_1_out};  // Bit_Extender bit_extender_3
  assign controlled_buffer_15_out = or_1_out ? adder_1_cout : 1'bz;  // Controlled_Buffer controlled_buffer_15
  assign controlled_buffer_15_out = or_2_out ? subtractor_1_bout : 1'bz;  // Controlled_Buffer controlled_buffer_16
  Pull_Resistor pull_resistor_1 (.node(controlled_buffer_1_out));
  Pull_Resistor pull_resistor_2 (.node(controlled_buffer_15_out));
  or or_4 (SetCarry, or_1_out, or_2_out);
  Comparator #(.mode("unsigned"), .width(32)) comparator_1 (
    .a(controlled_buffer_1_out), .b({32{1'b0}}), .eq(Zero));  // open: gt, lt
  and and_4 (CarryOut, controlled_buffer_15_out, SetCarry);
endmodule

module alu64 (
  input  [63:0] A,
  input  [63:0] B,
  input  CarryIn,
  input  [7:0] Op,
  output [63:0] R,
  output Zero,
  output CarryOut,
  output SetCarry,
  output SetR
);

  wire adder_1_cout, and_1_out, and_2_out, controlled_buffer_15_out, decoder_1_out0, decoder_1_out1,
       decoder_1_out2, decoder_1_out3, decoder_1_out4, decoder_1_out5, decoder_1_out6, decoder_1_out7,
       decoder_1_out8, decoder_1_out9, decoder_1_out10, decoder_1_out11, decoder_1_out12, decoder_1_out13,
       decoder_1_out14, decoder_1_out15, decoder_1_out16, or_1_out, or_2_out, subtractor_1_bout;
  wire [63:0] adder_1_out, and_3_out, divider_1_out, divider_1_rem, divider_2_out, divider_2_rem,
       multiplexer_1_out, multiplier_1_cout, multiplier_1_out, multiplier_2_cout, multiplier_2_out,
       negator_1_out, not_1_out, or_3_out, subtractor_1_out;

  Multiplexer #(.enable("false"), .width(64)) multiplexer_1 (
    .in0(B), .in1({64{1'b0}}), .out(multiplexer_1_out), .sel(Op[7]));
  Decoder #(.select(5)) decoder_1 (
    .out0(decoder_1_out0), .out1(decoder_1_out1), .out2(decoder_1_out2), .out3(decoder_1_out3),
    .out4(decoder_1_out4), .out5(decoder_1_out5), .out6(decoder_1_out6), .out7(decoder_1_out7),
    .out8(decoder_1_out8), .out9(decoder_1_out9), .out10(decoder_1_out10), .out11(decoder_1_out11),
    .out12(decoder_1_out12), .out13(decoder_1_out13), .out14(decoder_1_out14), .out15(decoder_1_out15),
    .out16(decoder_1_out16), .sel(Op[4:0]));  // open: out17, out18, out19, out20, out21, out22, out23, out24, out25, out26, out27, out28, out29, out30, out31, en
  and and_1 (and_1_out, decoder_1_out14, CarryIn);
  and and_2 (and_2_out, decoder_1_out15, CarryIn);
  or or_1 (or_1_out, decoder_1_out14, decoder_1_out3);
  or or_2 (or_2_out, decoder_1_out15, decoder_1_out16, decoder_1_out4);
  assign not_1_out = ~A;  // NOT_Gate not_1, 64 bits wide
  assign R = decoder_1_out0 ? not_1_out : 64'bz;  // Controlled_Buffer controlled_buffer_1
  assign and_3_out = A & multiplexer_1_out;  // AND_Gate and_3, 64 bits wide
  assign R = decoder_1_out1 ? and_3_out : 64'bz;  // Controlled_Buffer controlled_buffer_2
  assign or_3_out = A | multiplexer_1_out;  // OR_Gate or_3, 64 bits wide
  assign R = decoder_1_out2 ? or_3_out : 64'bz;  // Controlled_Buffer controlled_buffer_3
  assign R = or_1_out ? adder_1_out : 64'bz;  // Controlled_Buffer controlled_buffer_4
  Adder #(.width(64)) adder_1 (.a(A), .b(multiplexer_1_out), .out(adder_1_out), .cin(and_1_out), .cout(adder_1_cout));
  assign R = or_2_out ? subtractor_1_out : 64'bz;  // Controlled_Buffer controlled_buffer_5
  Subtractor #(.width(64)) subtractor_1 (
    .a(A), .b(multiplexer_1_out), .out(subtractor_1_out), .bin(and_2_out), .bout(subtractor_1_bout));
  assign R = decoder_1_out5 ? multiplier_1_out : 64'bz;  // Controlled_Buffer controlled_buffer_6
  Multiplier #(.width(64)) multiplier_1 (
    .a(A), .b(multiplexer_1_out), .out(multiplier_1_out), .cout(multiplier_1_cout));  // open: cin
  assign R = decoder_1_out6 ? multiplier_1_cout : 64'bz;  // Controlled_Buffer controlled_buffer_7
  assign R = decoder_1_out7 ? multiplier_2_out : 64'bz;  // Controlled_Buffer controlled_buffer_8
  Multiplier #(.mode("twosComplement"), .width(64)) multiplier_2 (
    .a(A), .b(multiplexer_1_out), .out(multiplier_2_out), .cout(multiplier_2_cout));  // open: cin
  assign R = decoder_1_out8 ? multiplier_2_cout : 64'bz;  // Controlled_Buffer controlled_buffer_9
  assign R = decoder_1_out9 ? divider_1_out : 64'bz;  // Controlled_Buffer controlled_buffer_10
  Divider #(.width(64)) divider_1 (
    .a(A), .b(multiplexer_1_out), .out(divider_1_out), .rem(divider_1_rem));  // open: upper
  assign R = decoder_1_out10 ? divider_1_rem : 64'bz;  // Controlled_Buffer controlled_buffer_11
  assign R = decoder_1_out11 ? divider_2_out : 64'bz;  // Controlled_Buffer controlled_buffer_12
  Divider #(.mode("twosComplement"), .width(64)) divider_2 (
    .a(A), .b(multiplexer_1_out), .out(divider_2_out), .rem(divider_2_rem));  // open: upper
  assign R = decoder_1_out12 ? divider_2_rem : 64'bz;  // Controlled_Buffer controlled_buffer_13
  assign R = decoder_1_out13 ? negator_1_out : 64'bz;  // Controlled_Buffer controlled_buffer_14
  Negator #(.width(64)) negator_1 (.in(A), .out(negator_1_out));
  not not_2 (SetR, decoder_1_out16);
  Pull_Resistor pull_resistor_1 (.node(R));
  assign controlled_buffer_15_out = or_1_out ? adder_1_cout : 1'bz;  // Controlled_Buffer controlled_buffer_15
  assign controlled_buffer_15_out = or_2_out ? subtractor_1_bout : 1'bz;  // Controlled_Buffer controlled_buffer_16
  Pull_Resistor pull_resistor_2 (.node(controlled_buffer_15_out));
  or or_4 (SetCarry, or_1_out, or_2_out);
  Comparator #(.mode("unsigned"), .width(64)) comparator_1 (.a(R), .b({64{1'b0}}), .eq(Zero));  // open: gt, lt
  and and_4 (CarryOut, controlled_buffer_15_out, SetCarry);
endmodule

module pciconfhandler (
  input  Clock,
  input  Wr,
  input  ConfEn,
  input  [7:0] ConfOffset,
  input  [15:0] DevNo,
  input  [15:0] DevNoBus,
  input  [63:0] DataIn,
  input  [63:0] Address,
  input  [63:0] Bar_LenMask_0,
  input  [63:0] Bar_LenMask_1,
  input  [63:0] Bar_LenMask_2,
  input  [63:0] Bar_LenMask_3,
  input  [63:0] Bar_LenMask_4,
  input  [63:0] Bar_LenMask_5,
  input  [63:0] Bar_LenMask_6,
  input  [63:0] Bar_LenMask_7,
  output NotBAR,
  output [63:0] Dout,
  output Bar0,
  output Bar1,
  output Bar2,
  output Bar3,
  output Bar4,
  output Bar5,
  output Bar6,
  output Bar7
);

  wire and_30_out, Bar_En_Write, Bar_Write_0, Bar_Write_1, Bar_Write_2, Bar_Write_3, Bar_Write_4,
       Bar_Write_5, Bar_Write_6, Bar_Write_7, comparator_2_gt, comparator_2_lt, comparator_3_gt,
       comparator_3_lt, comparator_4_eq, comparator_5_eq, comparator_6_eq, comparator_7_eq, comparator_8_eq,
       comparator_9_eq, comparator_10_eq, comparator_11_eq, comparator_12_eq, IsBAR, not_1_out, or_1_out,
       OurConf, Rd, Wr_t;
  wire [7:0] bit_extender_1_out, register_1_q, subtractor_1_out;
  wire [63:0] and_1_out, and_2_out, and_3_out, and_4_out, and_5_out, and_6_out, and_7_out, and_8_out,
       and_10_out, and_11_out, and_12_out, and_13_out, and_14_out, and_15_out, and_16_out, and_17_out,
       Bar_LenMask_0_t, Bar_LenMask_1_t, Bar_LenMask_2_t, Bar_LenMask_3_t, Bar_LenMask_4_t, Bar_LenMask_5_t,
       Bar_LenMask_6_t, Bar_LenMask_7_t, register_2_q, register_3_q, register_4_q, register_5_q,
       register_6_q, register_7_q, register_8_q, register_9_q;

  assign and_1_out = ~Bar_LenMask_0 & DataIn;  // AND_Gate and_1, 64 bits wide
  assign and_2_out = ~Bar_LenMask_1 & DataIn;  // AND_Gate and_2, 64 bits wide
  assign and_3_out = ~Bar_LenMask_2 & DataIn;  // AND_Gate and_3, 64 bits wide
  assign and_4_out = ~Bar_LenMask_3 & DataIn;  // AND_Gate and_4, 64 bits wide
  assign and_5_out = ~Bar_LenMask_4 & DataIn;  // AND_Gate and_5, 64 bits wide
  assign and_6_out = ~Bar_LenMask_5 & DataIn;  // AND_Gate and_6, 64 bits wide
  assign and_7_out = ~Bar_LenMask_6 & DataIn;  // AND_Gate and_7, 64 bits wide
  assign and_8_out = ~Bar_LenMask_7 & DataIn;  // AND_Gate and_8, 64 bits wide
  Comparator #(.width(16)) comparator_1 (.a(DevNo), .b(DevNoBus), .eq(OurConf));  // open: gt, lt
  Bit_Extender #(.in_width(64), .out_width(8), .\type ("zero")) bit_extender_1 (.in(DataIn), .out(bit_extender_1_out));
  not not_1 (not_1_out, Wr);
  and and_9 (Wr_t, Wr, ConfEn);
  Register register_1 (.D(bit_extender_1_out), .en(Bar_En_Write), .Q(register_1_q), .clk(Clock));  // open: clr
  assign and_10_out = Address & Bar_LenMask_0_t;  // AND_Gate and_10, 64 bits wide
  Register #(.width(64)) register_2 (.D(and_1_out), .en(Bar_Write_0), .Q(register_2_q), .clk(Clock));  // open: clr
  assign and_11_out = Address & Bar_LenMask_1_t;  // AND_Gate and_11, 64 bits wide
  Register #(.width(64)) register_3 (.D(and_2_out), .en(Bar_Write_1), .Q(register_3_q), .clk(Clock));  // open: clr
  assign and_12_out = Address & Bar_LenMask_2_t;  // AND_Gate and_12, 64 bits wide
  Register #(.width(64)) register_4 (.D(and_3_out), .en(Bar_Write_2), .Q(register_4_q), .clk(Clock));  // open: clr
  assign and_13_out = Address & Bar_LenMask_3_t;  // AND_Gate and_13, 64 bits wide
  Register #(.width(64)) register_5 (.D(and_4_out), .en(Bar_Write_3), .Q(register_5_q), .clk(Clock));  // open: clr
  assign and_14_out = Address & Bar_LenMask_4_t;  // AND_Gate and_14, 64 bits wide
  Register #(.width(64)) register_6 (.D(and_5_out), .en(Bar_Write_3), .Q(register_6_q), .clk(Clock));  // open: clr
  assign and_15_out = Address & Bar_LenMask_5_t;  // AND_Gate and_15, 64 bits wide
  Register #(.width(64)) register_7 (.D(and_6_out), .en(Bar_Write_3), .Q(register_7_q), .clk(Clock));  // open: clr
  assign and_16_out = Address & Bar_LenMask_6_t;  // AND_Gate and_16, 64 bits wide
  assign and_17_out = Address & Bar_LenMask_7_t;  // AND_Gate and_17, 64 bits wide
  and and_18 (Rd, ConfEn, not_1_out);
  Register #(.width(64)) register_8 (.D(and_7_out), .en(Bar_Write_3), .Q(register_8_q), .clk(Clock));  // open: clr
  Register #(.width(64)) register_9 (.D(and_8_out), .en(Bar_Write_3), .Q(register_9_q), .clk(Clock));  // open: clr
  Comparator comparator_2 (.a(ConfOffset), .b(8'h11), .gt(comparator_2_gt), .lt(comparator_2_lt));  // open: eq
  Comparator comparator_3 (.a(ConfOffset), .b(8'h52), .gt(comparator_3_gt), .lt(comparator_3_lt));  // open: eq
  Comparator #(.width(64)) comparator_4 (.a(and_10_out), .b(register_2_q), .eq(comparator_4_eq));  // open: gt, lt
  Comparator #(.width(64)) comparator_5 (.a(and_11_out), .b(register_3_q), .eq(comparator_5_eq));  // open: gt, lt
  Comparator #(.width(64)) comparator_6 (.a(and_12_out), .b(register_4_q), .eq(comparator_6_eq));  // open: gt, lt
  Comparator #(.width(64)) comparator_7 (.a(and_13_out), .b(register_5_q), .eq(comparator_7_eq));  // open: gt, lt
  Comparator #(.width(64)) comparator_8 (.a(and_14_out), .b(register_6_q), .eq(comparator_8_eq));  // open: gt, lt
  Comparator #(.width(64)) comparator_9 (.a(and_15_out), .b(register_7_q), .eq(comparator_9_eq));  // open: gt, lt
  Comparator #(.width(64)) comparator_10 (.a(and_16_out), .b(register_8_q), .eq(comparator_10_eq));  // open: gt, lt
  Comparator #(.width(64)) comparator_11 (.a(and_17_out), .b(register_9_q), .eq(comparator_11_eq));  // open: gt, lt
  and and_19 (IsBAR, OurConf, comparator_2_gt, comparator_3_lt);
  or or_1 (or_1_out, comparator_3_gt, comparator_2_lt);
  // AND_Gate and_20 has open pins: in0=or_1_out, in1=OurConf, out=open
  and and_21 (Bar0, register_1_q[0], comparator_4_eq);
  and and_22 (Bar1, register_1_q[1], comparator_5_eq);
  and and_23 (Bar2, register_1_q[2], comparator_6_eq);
  and and_24 (Bar3, register_1_q[3], comparator_7_eq);
  and and_25 (Bar4, register_1_q[4], comparator_8_eq);
  and and_26 (Bar5, register_1_q[5], comparator_9_eq);
  and and_27 (Bar6, register_1_q[6], comparator_10_eq);
  and and_28 (Bar7, register_1_q[7], comparator_11_eq);
  Comparator comparator_12 (.a(ConfOffset), .b(8'h11), .eq(comparator_12_eq));  // open: gt, lt
  nor nor_1 (NotBAR, comparator_12_eq, IsBAR);
  and and_29 (Bar_En_Write, comparator_12_eq, Wr_t);
  Subtractor subtractor_1 (.a(ConfOffset), .b(8'h12), .out(subtractor_1_out));  // open: bin, bout
  Demultiplexer #(.select(3)) demultiplexer_1 (
    .out0(Bar_Write_0), .out1(Bar_Write_1), .out2(Bar_Write_2), .out3(Bar_Write_3), .out4(Bar_Write_4),
    .out5(Bar_Write_5), .out6(Bar_Write_6), .out7(Bar_Write_7), .in(Wr_t), .sel(subtractor_1_out[5:3]),
    .en(IsBAR));
  Multiplexer #(.disabled("Z"), .select(3), .width(64)) multiplexer_1 (
    .in0(Bar_LenMask_0), .in1(Bar_LenMask_1), .in2(Bar_LenMask_2), .in3(Bar_LenMask_3), .in4(Bar_LenMask_4),
    .in5(Bar_LenMask_5), .in6(Bar_LenMask_6), .in7(Bar_LenMask_7), .out(Dout), .sel(subtractor_1_out[5:3]),
    .en(and_30_out));
  and and_30 (and_30_out, IsBAR, Rd);

  // Other names for the same wires on the sheet: Bar_Len_Mask_0[63:0] = Bar_LenMask_0;
  //   Bar_Len_Mask_1[63:0] = Bar_LenMask_1; Bar_Len_Mask_2[63:0] = Bar_LenMask_2;
  //   Bar_Len_Mask_3[63:0] = Bar_LenMask_3; Bar_Len_Mask_4[63:0] = Bar_LenMask_4;
  //   Bar_Len_Mask_5[63:0] = Bar_LenMask_5; Bar_Len_Mask_6[63:0] = Bar_LenMask_6;
  //   Bar_Len_Mask_7[63:0] = Bar_LenMask_7
endmodule

module cam16 (
  input  [63:0] CmpData,
  input  [63:0] WrData,
  input  Wr,
  input  Reset,
  input  [3:0] Addr,
  output [3:0] MatchAddr,
  output MatchFound
);

  wire comparator_1_eq, comparator_2_eq, comparator_3_eq, comparator_4_eq, comparator_5_eq, comparator_6_eq,
       comparator_7_eq, comparator_8_eq, comparator_9_eq, comparator_10_eq, comparator_11_eq,
       comparator_12_eq, comparator_13_eq, comparator_14_eq, comparator_15_eq, comparator_16_eq,
       decoder_1_out0, decoder_1_out1, decoder_1_out2, decoder_1_out3, decoder_1_out4, decoder_1_out5,
       decoder_1_out6, decoder_1_out7, decoder_1_out8, decoder_1_out9, decoder_1_out10, decoder_1_out11,
       decoder_1_out12, decoder_1_out13, decoder_1_out14, decoder_1_out15;
  wire [63:0] register_1_q, register_2_q, register_3_q, register_4_q, register_5_q, register_6_q,
       register_7_q, register_8_q, register_9_q, register_10_q, register_11_q, register_12_q, register_13_q,
       register_14_q, register_15_q, register_16_q;

  Decoder #(.enable("false"), .select(4)) decoder_1 (
    .out0(decoder_1_out0), .out1(decoder_1_out1), .out2(decoder_1_out2), .out3(decoder_1_out3),
    .out4(decoder_1_out4), .out5(decoder_1_out5), .out6(decoder_1_out6), .out7(decoder_1_out7),
    .out8(decoder_1_out8), .out9(decoder_1_out9), .out10(decoder_1_out10), .out11(decoder_1_out11),
    .out12(decoder_1_out12), .out13(decoder_1_out13), .out14(decoder_1_out14), .out15(decoder_1_out15),
    .sel(Addr));
  Register #(.trigger("falling"), .width(64)) register_1 (
    .D(WrData), .en(decoder_1_out0), .Q(register_1_q), .clk(Wr), .clr(Reset));
  Register #(.trigger("falling"), .width(64)) register_2 (
    .D(WrData), .en(decoder_1_out1), .Q(register_2_q), .clk(Wr), .clr(Reset));
  Register #(.trigger("falling"), .width(64)) register_3 (
    .D(WrData), .en(decoder_1_out2), .Q(register_3_q), .clk(Wr), .clr(Reset));
  Register #(.trigger("falling"), .width(64)) register_4 (
    .D(WrData), .en(decoder_1_out3), .Q(register_4_q), .clk(Wr), .clr(Reset));
  Register #(.trigger("falling"), .width(64)) register_5 (
    .D(WrData), .en(decoder_1_out4), .Q(register_5_q), .clk(Wr), .clr(Reset));
  Register #(.trigger("falling"), .width(64)) register_6 (
    .D(WrData), .en(decoder_1_out5), .Q(register_6_q), .clk(Wr), .clr(Reset));
  Register #(.trigger("falling"), .width(64)) register_7 (
    .D(WrData), .en(decoder_1_out6), .Q(register_7_q), .clk(Wr), .clr(Reset));
  Register #(.trigger("falling"), .width(64)) register_8 (
    .D(WrData), .en(decoder_1_out7), .Q(register_8_q), .clk(Wr), .clr(Reset));
  Register #(.trigger("falling"), .width(64)) register_9 (
    .D(WrData), .en(decoder_1_out8), .Q(register_9_q), .clk(Wr), .clr(Reset));
  Register #(.trigger("falling"), .width(64)) register_10 (
    .D(WrData), .en(decoder_1_out9), .Q(register_10_q), .clk(Wr), .clr(Reset));
  Register #(.trigger("falling"), .width(64)) register_11 (
    .D(WrData), .en(decoder_1_out10), .Q(register_11_q), .clk(Wr), .clr(Reset));
  Register #(.trigger("falling"), .width(64)) register_12 (
    .D(WrData), .en(decoder_1_out11), .Q(register_12_q), .clk(Wr), .clr(Reset));
  Register #(.trigger("falling"), .width(64)) register_13 (
    .D(WrData), .en(decoder_1_out12), .Q(register_13_q), .clk(Wr), .clr(Reset));
  Register #(.trigger("falling"), .width(64)) register_14 (
    .D(WrData), .en(decoder_1_out13), .Q(register_14_q), .clk(Wr), .clr(Reset));
  Register #(.trigger("falling"), .width(64)) register_15 (
    .D(WrData), .en(decoder_1_out14), .Q(register_15_q), .clk(Wr), .clr(Reset));
  Register #(.trigger("falling"), .width(64)) register_16 (
    .D(WrData), .en(decoder_1_out15), .Q(register_16_q), .clk(Wr), .clr(Reset));
  Comparator #(.width(64)) comparator_1 (.a(CmpData), .b(register_1_q), .eq(comparator_1_eq));  // open: gt, lt
  Comparator #(.width(64)) comparator_2 (.a(CmpData), .b(register_2_q), .eq(comparator_2_eq));  // open: gt, lt
  Comparator #(.width(64)) comparator_3 (.a(CmpData), .b(register_3_q), .eq(comparator_3_eq));  // open: gt, lt
  Comparator #(.width(64)) comparator_4 (.a(CmpData), .b(register_4_q), .eq(comparator_4_eq));  // open: gt, lt
  Comparator #(.width(64)) comparator_5 (.a(CmpData), .b(register_5_q), .eq(comparator_5_eq));  // open: gt, lt
  Comparator #(.width(64)) comparator_6 (.a(CmpData), .b(register_6_q), .eq(comparator_6_eq));  // open: gt, lt
  Comparator #(.width(64)) comparator_7 (.a(CmpData), .b(register_7_q), .eq(comparator_7_eq));  // open: gt, lt
  Comparator #(.width(64)) comparator_8 (.a(CmpData), .b(register_8_q), .eq(comparator_8_eq));  // open: gt, lt
  Comparator #(.width(64)) comparator_9 (.a(CmpData), .b(register_9_q), .eq(comparator_9_eq));  // open: gt, lt
  Comparator #(.width(64)) comparator_10 (.a(CmpData), .b(register_10_q), .eq(comparator_10_eq));  // open: gt, lt
  Comparator #(.width(64)) comparator_11 (.a(CmpData), .b(register_11_q), .eq(comparator_11_eq));  // open: gt, lt
  Comparator #(.width(64)) comparator_12 (.a(CmpData), .b(register_12_q), .eq(comparator_12_eq));  // open: gt, lt
  Comparator #(.width(64)) comparator_13 (.a(CmpData), .b(register_13_q), .eq(comparator_13_eq));  // open: gt, lt
  Comparator #(.width(64)) comparator_14 (.a(CmpData), .b(register_14_q), .eq(comparator_14_eq));  // open: gt, lt
  Comparator #(.width(64)) comparator_15 (.a(CmpData), .b(register_15_q), .eq(comparator_15_eq));  // open: gt, lt
  Comparator #(.width(64)) comparator_16 (.a(CmpData), .b(register_16_q), .eq(comparator_16_eq));  // open: gt, lt
  Priority_Encoder #(.select(4)) priority_encoder_1 (
    .in0(comparator_1_eq), .in1(comparator_2_eq), .in2(comparator_3_eq), .in3(comparator_4_eq),
    .in4(comparator_5_eq), .in5(comparator_6_eq), .in6(comparator_7_eq), .in7(comparator_8_eq),
    .in8(comparator_9_eq), .in9(comparator_10_eq), .in10(comparator_11_eq), .in11(comparator_12_eq),
    .in12(comparator_13_eq), .in13(comparator_14_eq), .in14(comparator_15_eq), .in15(comparator_16_eq),
    .out(MatchAddr), .gs(MatchFound));  // open: en_out, en_in
endmodule

module cam256 (
  input  [63:0] CmpData,
  input  [63:0] WrData,
  input  Wr,
  input  Reset,
  input  [7:0] Addr,
  output [7:0] MatchAddr,
  output MatchFound
);

  wire cam16_1_matchfound, cam16_2_matchfound, cam16_3_matchfound, cam16_4_matchfound, cam16_5_matchfound,
       cam16_6_matchfound, cam16_7_matchfound, cam16_8_matchfound, cam16_9_matchfound, cam16_10_matchfound,
       cam16_11_matchfound, cam16_12_matchfound, cam16_13_matchfound, cam16_14_matchfound,
       cam16_15_matchfound, cam16_16_matchfound, demultiplexer_1_out0, demultiplexer_1_out1,
       demultiplexer_1_out2, demultiplexer_1_out3, demultiplexer_1_out4, demultiplexer_1_out5,
       demultiplexer_1_out6, demultiplexer_1_out7, demultiplexer_1_out8, demultiplexer_1_out9,
       demultiplexer_1_out10, demultiplexer_1_out11, demultiplexer_1_out12, demultiplexer_1_out13,
       demultiplexer_1_out14, demultiplexer_1_out15;
  wire [3:0] cam16_1_matchaddr, cam16_2_matchaddr, cam16_3_matchaddr, cam16_4_matchaddr, cam16_5_matchaddr,
       cam16_6_matchaddr, cam16_7_matchaddr, cam16_8_matchaddr, cam16_9_matchaddr, cam16_10_matchaddr,
       cam16_11_matchaddr, cam16_12_matchaddr, cam16_13_matchaddr, cam16_14_matchaddr, cam16_15_matchaddr,
       cam16_16_matchaddr;

  Demultiplexer #(.enable("false"), .select(4)) demultiplexer_1 (
    .out0(demultiplexer_1_out0), .out1(demultiplexer_1_out1), .out2(demultiplexer_1_out2),
    .out3(demultiplexer_1_out3), .out4(demultiplexer_1_out4), .out5(demultiplexer_1_out5),
    .out6(demultiplexer_1_out6), .out7(demultiplexer_1_out7), .out8(demultiplexer_1_out8),
    .out9(demultiplexer_1_out9), .out10(demultiplexer_1_out10), .out11(demultiplexer_1_out11),
    .out12(demultiplexer_1_out12), .out13(demultiplexer_1_out13), .out14(demultiplexer_1_out14),
    .out15(demultiplexer_1_out15), .in(Wr), .sel(Addr[7:4]));
  cam16 cam16_1 (
    .CmpData(CmpData), .WrData(WrData), .Wr(demultiplexer_1_out0), .Reset(Reset), .Addr(Addr[3:0]),
    .MatchAddr(cam16_1_matchaddr), .MatchFound(cam16_1_matchfound));
  cam16 cam16_2 (
    .CmpData(CmpData), .WrData(WrData), .Wr(demultiplexer_1_out1), .Reset(Reset), .Addr(Addr[3:0]),
    .MatchAddr(cam16_2_matchaddr), .MatchFound(cam16_2_matchfound));
  cam16 cam16_3 (
    .CmpData(CmpData), .WrData(WrData), .Wr(demultiplexer_1_out2), .Reset(Reset), .Addr(Addr[3:0]),
    .MatchAddr(cam16_3_matchaddr), .MatchFound(cam16_3_matchfound));
  cam16 cam16_4 (
    .CmpData(CmpData), .WrData(WrData), .Wr(demultiplexer_1_out3), .Reset(Reset), .Addr(Addr[3:0]),
    .MatchAddr(cam16_4_matchaddr), .MatchFound(cam16_4_matchfound));
  cam16 cam16_5 (
    .CmpData(CmpData), .WrData(WrData), .Wr(demultiplexer_1_out4), .Reset(Reset), .Addr(Addr[3:0]),
    .MatchAddr(cam16_5_matchaddr), .MatchFound(cam16_5_matchfound));
  cam16 cam16_6 (
    .CmpData(CmpData), .WrData(WrData), .Wr(demultiplexer_1_out5), .Reset(Reset), .Addr(Addr[3:0]),
    .MatchAddr(cam16_6_matchaddr), .MatchFound(cam16_6_matchfound));
  cam16 cam16_7 (
    .CmpData(CmpData), .WrData(WrData), .Wr(demultiplexer_1_out6), .Reset(Reset), .Addr(Addr[3:0]),
    .MatchAddr(cam16_7_matchaddr), .MatchFound(cam16_7_matchfound));
  cam16 cam16_8 (
    .CmpData(CmpData), .WrData(WrData), .Wr(demultiplexer_1_out7), .Reset(Reset), .Addr(Addr[3:0]),
    .MatchAddr(cam16_8_matchaddr), .MatchFound(cam16_8_matchfound));
  cam16 cam16_9 (
    .CmpData(CmpData), .WrData(WrData), .Wr(demultiplexer_1_out8), .Reset(Reset), .Addr(Addr[3:0]),
    .MatchAddr(cam16_9_matchaddr), .MatchFound(cam16_9_matchfound));
  cam16 cam16_10 (
    .CmpData(CmpData), .WrData(WrData), .Wr(demultiplexer_1_out9), .Reset(Reset), .Addr(Addr[3:0]),
    .MatchAddr(cam16_10_matchaddr), .MatchFound(cam16_10_matchfound));
  cam16 cam16_11 (
    .CmpData(CmpData), .WrData(WrData), .Wr(demultiplexer_1_out10), .Reset(Reset), .Addr(Addr[3:0]),
    .MatchAddr(cam16_11_matchaddr), .MatchFound(cam16_11_matchfound));
  cam16 cam16_12 (
    .CmpData(CmpData), .WrData(WrData), .Wr(demultiplexer_1_out11), .Reset(Reset), .Addr(Addr[3:0]),
    .MatchAddr(cam16_12_matchaddr), .MatchFound(cam16_12_matchfound));
  cam16 cam16_13 (
    .CmpData(CmpData), .WrData(WrData), .Wr(demultiplexer_1_out12), .Reset(Reset), .Addr(Addr[3:0]),
    .MatchAddr(cam16_13_matchaddr), .MatchFound(cam16_13_matchfound));
  cam16 cam16_14 (
    .CmpData(CmpData), .WrData(WrData), .Wr(demultiplexer_1_out13), .Reset(Reset), .Addr(Addr[3:0]),
    .MatchAddr(cam16_14_matchaddr), .MatchFound(cam16_14_matchfound));
  cam16 cam16_15 (
    .CmpData(CmpData), .WrData(WrData), .Wr(demultiplexer_1_out14), .Reset(Reset), .Addr(Addr[3:0]),
    .MatchAddr(cam16_15_matchaddr), .MatchFound(cam16_15_matchfound));
  cam16 cam16_16 (
    .CmpData(CmpData), .WrData(WrData), .Wr(demultiplexer_1_out15), .Reset(Reset), .Addr(Addr[3:0]),
    .MatchAddr(cam16_16_matchaddr), .MatchFound(cam16_16_matchfound));
  Multiplexer #(.enable("false"), .select(4), .width(4)) multiplexer_1 (
    .in0(cam16_1_matchaddr), .in1(cam16_2_matchaddr), .in2(cam16_3_matchaddr), .in3(cam16_4_matchaddr),
    .in4(cam16_5_matchaddr), .in5(cam16_6_matchaddr), .in6(cam16_7_matchaddr), .in7(cam16_8_matchaddr),
    .in8(cam16_9_matchaddr), .in9(cam16_10_matchaddr), .in10(cam16_11_matchaddr), .in11(cam16_12_matchaddr),
    .in12(cam16_13_matchaddr), .in13(cam16_14_matchaddr), .in14(cam16_15_matchaddr),
    .in15(cam16_16_matchaddr), .out(MatchAddr[3:0]), .sel(MatchAddr[7:4]));
  Priority_Encoder #(.select(4)) priority_encoder_1 (
    .in0(cam16_1_matchfound), .in1(cam16_2_matchfound), .in2(cam16_3_matchfound), .in3(cam16_4_matchfound),
    .in4(cam16_5_matchfound), .in5(cam16_6_matchfound), .in6(cam16_7_matchfound), .in7(cam16_8_matchfound),
    .in8(cam16_9_matchfound), .in9(cam16_10_matchfound), .in10(cam16_11_matchfound),
    .in11(cam16_12_matchfound), .in12(cam16_13_matchfound), .in13(cam16_14_matchfound),
    .in14(cam16_15_matchfound), .in15(cam16_16_matchfound), .out(MatchAddr[7:4]), .gs(MatchFound));  // open: en_out, en_in
endmodule

module cam4k (
  input  [63:0] CmpData,
  input  [63:0] WrData,
  input  Wr,
  input  Reset,
  input  [11:0] Addr,
  output [11:0] MatchAddr,
  output MatchFound
);

  wire cam256_1_matchfound, cam256_2_matchfound, cam256_3_matchfound, cam256_4_matchfound,
       cam256_5_matchfound, cam256_6_matchfound, cam256_7_matchfound, cam256_8_matchfound,
       cam256_9_matchfound, cam256_10_matchfound, cam256_11_matchfound, cam256_12_matchfound,
       cam256_13_matchfound, cam256_14_matchfound, cam256_15_matchfound, cam256_16_matchfound,
       demultiplexer_1_out0, demultiplexer_1_out1, demultiplexer_1_out2, demultiplexer_1_out3,
       demultiplexer_1_out4, demultiplexer_1_out5, demultiplexer_1_out6, demultiplexer_1_out7,
       demultiplexer_1_out8, demultiplexer_1_out9, demultiplexer_1_out10, demultiplexer_1_out11,
       demultiplexer_1_out12, demultiplexer_1_out13, demultiplexer_1_out14, demultiplexer_1_out15;
  wire [7:0] cam256_1_matchaddr, cam256_2_matchaddr, cam256_3_matchaddr, cam256_4_matchaddr,
       cam256_5_matchaddr, cam256_6_matchaddr, cam256_7_matchaddr, cam256_8_matchaddr, cam256_9_matchaddr,
       cam256_10_matchaddr, cam256_11_matchaddr, cam256_12_matchaddr, cam256_13_matchaddr,
       cam256_14_matchaddr, cam256_15_matchaddr, cam256_16_matchaddr;

  Demultiplexer #(.enable("false"), .select(4)) demultiplexer_1 (
    .out0(demultiplexer_1_out0), .out1(demultiplexer_1_out1), .out2(demultiplexer_1_out2),
    .out3(demultiplexer_1_out3), .out4(demultiplexer_1_out4), .out5(demultiplexer_1_out5),
    .out6(demultiplexer_1_out6), .out7(demultiplexer_1_out7), .out8(demultiplexer_1_out8),
    .out9(demultiplexer_1_out9), .out10(demultiplexer_1_out10), .out11(demultiplexer_1_out11),
    .out12(demultiplexer_1_out12), .out13(demultiplexer_1_out13), .out14(demultiplexer_1_out14),
    .out15(demultiplexer_1_out15), .in(Wr), .sel(Addr[11:8]));
  cam256 cam256_1 (
    .CmpData(CmpData), .WrData(WrData), .Wr(demultiplexer_1_out0), .Reset(Reset), .Addr(Addr[7:0]),
    .MatchAddr(cam256_1_matchaddr), .MatchFound(cam256_1_matchfound));
  cam256 cam256_2 (
    .CmpData(CmpData), .WrData(WrData), .Wr(demultiplexer_1_out1), .Reset(Reset), .Addr(Addr[7:0]),
    .MatchAddr(cam256_2_matchaddr), .MatchFound(cam256_2_matchfound));
  cam256 cam256_3 (
    .CmpData(CmpData), .WrData(WrData), .Wr(demultiplexer_1_out2), .Reset(Reset), .Addr(Addr[7:0]),
    .MatchAddr(cam256_3_matchaddr), .MatchFound(cam256_3_matchfound));
  cam256 cam256_4 (
    .CmpData(CmpData), .WrData(WrData), .Wr(demultiplexer_1_out3), .Reset(Reset), .Addr(Addr[7:0]),
    .MatchAddr(cam256_4_matchaddr), .MatchFound(cam256_4_matchfound));
  cam256 cam256_5 (
    .CmpData(CmpData), .WrData(WrData), .Wr(demultiplexer_1_out4), .Reset(Reset), .Addr(Addr[7:0]),
    .MatchAddr(cam256_5_matchaddr), .MatchFound(cam256_5_matchfound));
  cam256 cam256_6 (
    .CmpData(CmpData), .WrData(WrData), .Wr(demultiplexer_1_out5), .Reset(Reset), .Addr(Addr[7:0]),
    .MatchAddr(cam256_6_matchaddr), .MatchFound(cam256_6_matchfound));
  cam256 cam256_7 (
    .CmpData(CmpData), .WrData(WrData), .Wr(demultiplexer_1_out6), .Reset(Reset), .Addr(Addr[7:0]),
    .MatchAddr(cam256_7_matchaddr), .MatchFound(cam256_7_matchfound));
  cam256 cam256_8 (
    .CmpData(CmpData), .WrData(WrData), .Wr(demultiplexer_1_out7), .Reset(Reset), .Addr(Addr[7:0]),
    .MatchAddr(cam256_8_matchaddr), .MatchFound(cam256_8_matchfound));
  cam256 cam256_9 (
    .CmpData(CmpData), .WrData(WrData), .Wr(demultiplexer_1_out8), .Reset(Reset), .Addr(Addr[7:0]),
    .MatchAddr(cam256_9_matchaddr), .MatchFound(cam256_9_matchfound));
  cam256 cam256_10 (
    .CmpData(CmpData), .WrData(WrData), .Wr(demultiplexer_1_out9), .Reset(Reset), .Addr(Addr[7:0]),
    .MatchAddr(cam256_10_matchaddr), .MatchFound(cam256_10_matchfound));
  cam256 cam256_11 (
    .CmpData(CmpData), .WrData(WrData), .Wr(demultiplexer_1_out10), .Reset(Reset), .Addr(Addr[7:0]),
    .MatchAddr(cam256_11_matchaddr), .MatchFound(cam256_11_matchfound));
  cam256 cam256_12 (
    .CmpData(CmpData), .WrData(WrData), .Wr(demultiplexer_1_out11), .Reset(Reset), .Addr(Addr[7:0]),
    .MatchAddr(cam256_12_matchaddr), .MatchFound(cam256_12_matchfound));
  cam256 cam256_13 (
    .CmpData(CmpData), .WrData(WrData), .Wr(demultiplexer_1_out12), .Reset(Reset), .Addr(Addr[7:0]),
    .MatchAddr(cam256_13_matchaddr), .MatchFound(cam256_13_matchfound));
  cam256 cam256_14 (
    .CmpData(CmpData), .WrData(WrData), .Wr(demultiplexer_1_out13), .Reset(Reset), .Addr(Addr[7:0]),
    .MatchAddr(cam256_14_matchaddr), .MatchFound(cam256_14_matchfound));
  cam256 cam256_15 (
    .CmpData(CmpData), .WrData(WrData), .Wr(demultiplexer_1_out14), .Reset(Reset), .Addr(Addr[7:0]),
    .MatchAddr(cam256_15_matchaddr), .MatchFound(cam256_15_matchfound));
  cam256 cam256_16 (
    .CmpData(CmpData), .WrData(WrData), .Wr(demultiplexer_1_out15), .Reset(Reset), .Addr(Addr[7:0]),
    .MatchAddr(cam256_16_matchaddr), .MatchFound(cam256_16_matchfound));
  Multiplexer #(.enable("false"), .select(4), .width(8)) multiplexer_1 (
    .in0(cam256_1_matchaddr), .in1(cam256_2_matchaddr), .in2(cam256_3_matchaddr), .in3(cam256_4_matchaddr),
    .in4(cam256_5_matchaddr), .in5(cam256_6_matchaddr), .in6(cam256_7_matchaddr), .in7(cam256_8_matchaddr),
    .in8(cam256_9_matchaddr), .in9(cam256_10_matchaddr), .in10(cam256_11_matchaddr),
    .in11(cam256_12_matchaddr), .in12(cam256_13_matchaddr), .in13(cam256_14_matchaddr),
    .in14(cam256_15_matchaddr), .in15(cam256_16_matchaddr), .out(MatchAddr[7:0]), .sel(MatchAddr[11:8]));
  Priority_Encoder #(.select(4)) priority_encoder_1 (
    .in0(cam256_1_matchfound), .in1(cam256_2_matchfound), .in2(cam256_3_matchfound),
    .in3(cam256_4_matchfound), .in4(cam256_5_matchfound), .in5(cam256_6_matchfound),
    .in6(cam256_7_matchfound), .in7(cam256_8_matchfound), .in8(cam256_9_matchfound),
    .in9(cam256_10_matchfound), .in10(cam256_11_matchfound), .in11(cam256_12_matchfound),
    .in12(cam256_13_matchfound), .in13(cam256_14_matchfound), .in14(cam256_15_matchfound),
    .in15(cam256_16_matchfound), .out(MatchAddr[11:8]), .gs(MatchFound));  // open: en_out, en_in
endmodule

module mmu (
  input  [63:0] AddrIn,
  input  Reset,
  input  MemCycle,
  input  Clock,
  input  [63:0] Din,
  input  [63:0] PL6P_Data,
  input  PL6P_Wr,
  output [63:0] AddrOut,
  output PageStructWalk,
  output PageFault,
  output [7:0] Lout
);

  wire and_1_out, and_2_out, and_3_out, buzzer_3_p3, comparator_1_eq, s_r_ff_1_q, TLBHit, TLBWr;
  wire [11:0] counter_1_q, lru4k_1_oldestaddr, MatchAddr, multiplexer_1_out, ram_1_dout, TLBWrAddr;
  wire [63:0] FetchedEntry, WalkAddress;
  wire [63:12] ram_1_dout_2;

  cam4k cam4k_1 (
    .CmpData({AddrIn[63:12], 12'h1}), .WrData({AddrIn[63:12], 12'h1}), .Wr(TLBWr), .Reset(Reset),
    .Addr(TLBWrAddr), .MatchAddr(MatchAddr), .MatchFound(TLBHit));
  Multiplexer #(.enable("false"), .width(12)) multiplexer_1 (
    .in0(MatchAddr), .in1(TLBWrAddr), .out(multiplexer_1_out), .sel(PageStructWalk));
  // Buzzer buzzer_1: pin names not known; wires that end beside it: MemCycle, 14'h14a
  and and_1 (and_1_out, TLBHit, Reset);
  and and_2 (and_2_out, MemCycle, Clock);
  RAM #(.addrWidth(12), .clearpin("true"), .dataWidth(64), .enables("line"), .trigger("falling")) ram_1 (
    .addr(multiplexer_1_out), .we(TLBWr), .clk(Clock), .din(FetchedEntry), .dout({ram_1_dout_2, ram_1_dout}),
    .clr(Reset));
  Counter #(.max('hfff), .trigger("falling"), .width(12)) counter_1 (
    .count(PageStructWalk), .Q(counter_1_q), .clk(TLBWr), .clr(Reset));  // open: load, D, carry, up
  lru4k lru4k_1 (.Reset(and_1_out), .MemCycle(and_2_out), .Addr(MatchAddr), .OldestAddr(lru4k_1_oldestaddr));
  Multiplexer #(.enable("false"), .width(12)) multiplexer_2 (
    .in0(counter_1_q), .in1(lru4k_1_oldestaddr), .out(TLBWrAddr), .sel(s_r_ff_1_q));
  pgfetcher pgfetcher_1 (
    .MemCycle(MemCycle), .TLBHit(TLBHit), .Reset(Reset), .Clock(Clock), .PgNoIn(AddrIn[63:12]), .Din(Din),
    .PL6P_Data(PL6P_Data), .PL6P_Wr(PL6P_Wr), .WalkAddress(WalkAddress), .TLBWr(TLBWr),
    .PGStructWalk(PageStructWalk), .FetchedEntry(FetchedEntry));
  Comparator #(.mode("unsigned"), .width(12)) comparator_1 (
    .a(counter_1_q), .b({12{1'b1}}), .eq(comparator_1_eq));  // open: gt, lt
  and and_3 (and_3_out, TLBWr, comparator_1_eq);
  S_R_Flip_Flop s_r_ff_1 (.Q(s_r_ff_1_q), .preset(and_3_out), .reset(Reset));  // open: S, clk, R, Qn
  Multiplexer #(.enable("false"), .width(64)) multiplexer_3 (
    .in0({ram_1_dout_2, AddrIn[11:0]}), .in1(WalkAddress), .out(AddrOut), .sel(PageStructWalk));
  // NOT_Gate not_1 has open pins: in=TLBHit, out=open
  and and_4 (PageFault, ~FetchedEntry[0], PageStructWalk);  // AND_Gate
  // Buzzer buzzer_2: pin names not known; wires that end beside it: 14'h106
  // Buzzer buzzer_3: pin names not known; wires that end beside it: PageFault, 14'h126, buzzer_3_p3, buzzer_3_p3
  // Buzzer buzzer_4: pin names not known; wires that end beside it: 14'h15d

  assign Lout = {8{1'b1}};

  // Other names for the same wires on the sheet: PgNoIn[51:0] = AddrIn[63:12]; PGStructWalk = PageStructWalk
endmodule

module lru16 (
  input  [31:0] PrevOldest,
  input  MemCycle,
  input  Reset,
  input  [3:0] Addr,
  output [31:0] OldestVal,
  output [3:0] OldestAddr
);

  wire and_1_out, and_2_out, and_3_out, and_4_out, and_5_out, and_6_out, and_7_out, and_8_out, and_9_out,
       and_10_out, and_11_out, and_12_out, and_13_out, and_14_out, and_15_out, comparator_1_lt,
       comparator_2_lt, comparator_3_lt, comparator_4_lt, comparator_5_lt, comparator_6_lt, comparator_7_lt,
       comparator_8_lt, comparator_9_lt, comparator_10_lt, comparator_11_lt, comparator_12_lt,
       comparator_13_lt, comparator_14_lt, comparator_15_lt, comparator_16_lt, decoder_1_out0,
       decoder_1_out1, decoder_1_out2, decoder_1_out3, decoder_1_out4, decoder_1_out5, decoder_1_out6,
       decoder_1_out7, decoder_1_out8, decoder_1_out9, decoder_1_out10, decoder_1_out11, decoder_1_out12,
       decoder_1_out13, decoder_1_out14, decoder_1_out15;
  wire [31:0] counter_1_q, counter_2_q, counter_3_q, counter_4_q, counter_5_q, counter_6_q, counter_7_q,
       counter_8_q, counter_9_q, counter_10_q, counter_11_q, counter_12_q, counter_13_q, counter_14_q,
       counter_15_q, counter_16_q;

  Decoder #(.select(4)) decoder_1 (
    .out0(decoder_1_out0), .out1(decoder_1_out1), .out2(decoder_1_out2), .out3(decoder_1_out3),
    .out4(decoder_1_out4), .out5(decoder_1_out5), .out6(decoder_1_out6), .out7(decoder_1_out7),
    .out8(decoder_1_out8), .out9(decoder_1_out9), .out10(decoder_1_out10), .out11(decoder_1_out11),
    .out12(decoder_1_out12), .out13(decoder_1_out13), .out14(decoder_1_out14), .out15(decoder_1_out15),
    .sel(Addr));  // open: en
  Counter #(.max('hffffffff), .width(32)) counter_1 (
    .load(decoder_1_out0), .D({32{1'b0}}), .Q(counter_1_q), .clk(MemCycle), .clr(Reset));  // open: count, carry, up
  Counter #(.max('hffffffff), .width(32)) counter_2 (
    .load(decoder_1_out1), .D({32{1'b0}}), .Q(counter_2_q), .clk(MemCycle), .clr(Reset));  // open: count, carry, up
  Counter #(.max('hffffffff), .width(32)) counter_3 (
    .load(decoder_1_out2), .D({32{1'b0}}), .Q(counter_3_q), .clk(MemCycle), .clr(Reset));  // open: count, carry, up
  Counter #(.max('hffffffff), .width(32)) counter_4 (
    .load(decoder_1_out3), .D({32{1'b0}}), .Q(counter_4_q), .clk(MemCycle), .clr(Reset));  // open: count, carry, up
  Counter #(.max('hffffffff), .width(32)) counter_5 (
    .load(decoder_1_out4), .D({32{1'b0}}), .Q(counter_5_q), .clk(MemCycle), .clr(Reset));  // open: count, carry, up
  Counter #(.max('hffffffff), .width(32)) counter_6 (
    .load(decoder_1_out5), .D({32{1'b0}}), .Q(counter_6_q), .clk(MemCycle), .clr(Reset));  // open: count, carry, up
  Counter #(.max('hffffffff), .width(32)) counter_7 (
    .load(decoder_1_out6), .D({32{1'b0}}), .Q(counter_7_q), .clk(MemCycle), .clr(Reset));  // open: count, carry, up
  Counter #(.max('hffffffff), .width(32)) counter_8 (
    .load(decoder_1_out7), .D({32{1'b0}}), .Q(counter_8_q), .clk(MemCycle), .clr(Reset));  // open: count, carry, up
  Counter #(.max('hffffffff), .width(32)) counter_9 (
    .load(decoder_1_out8), .D({32{1'b0}}), .Q(counter_9_q), .clk(MemCycle), .clr(Reset));  // open: count, carry, up
  Counter #(.max('hffffffff), .width(32)) counter_10 (
    .load(decoder_1_out9), .D({32{1'b0}}), .Q(counter_10_q), .clk(MemCycle), .clr(Reset));  // open: count, carry, up
  Counter #(.max('hffffffff), .width(32)) counter_11 (
    .load(decoder_1_out10), .D({32{1'b0}}), .Q(counter_11_q), .clk(MemCycle), .clr(Reset));  // open: count, carry, up
  Counter #(.max('hffffffff), .width(32)) counter_12 (
    .load(decoder_1_out11), .D({32{1'b0}}), .Q(counter_12_q), .clk(MemCycle), .clr(Reset));  // open: count, carry, up
  Counter #(.max('hffffffff), .width(32)) counter_13 (
    .load(decoder_1_out12), .D({32{1'b0}}), .Q(counter_13_q), .clk(MemCycle), .clr(Reset));  // open: count, carry, up
  Counter #(.max('hffffffff), .width(32)) counter_14 (
    .load(decoder_1_out13), .D({32{1'b0}}), .Q(counter_14_q), .clk(MemCycle), .clr(Reset));  // open: count, carry, up
  Counter #(.max('hffffffff), .width(32)) counter_15 (
    .load(decoder_1_out14), .D({32{1'b0}}), .Q(counter_15_q), .clk(MemCycle), .clr(Reset));  // open: count, carry, up
  Counter #(.max('hffffffff), .width(32)) counter_16 (
    .load(decoder_1_out15), .D({32{1'b0}}), .Q(counter_16_q), .clk(MemCycle), .clr(Reset));  // open: count, carry, up
  Comparator #(.mode("unsigned"), .width(32)) comparator_1 (
    .a(PrevOldest), .b(counter_1_q), .lt(comparator_1_lt));  // open: gt, eq
  Comparator #(.mode("unsigned"), .width(32)) comparator_2 (
    .a(PrevOldest), .b(counter_2_q), .lt(comparator_2_lt));  // open: gt, eq
  Comparator #(.mode("unsigned"), .width(32)) comparator_3 (
    .a(PrevOldest), .b(counter_3_q), .lt(comparator_3_lt));  // open: gt, eq
  Comparator #(.mode("unsigned"), .width(32)) comparator_4 (
    .a(PrevOldest), .b(counter_4_q), .lt(comparator_4_lt));  // open: gt, eq
  Comparator #(.mode("unsigned"), .width(32)) comparator_5 (
    .a(PrevOldest), .b(counter_5_q), .lt(comparator_5_lt));  // open: gt, eq
  Comparator #(.mode("unsigned"), .width(32)) comparator_6 (
    .a(PrevOldest), .b(counter_6_q), .lt(comparator_6_lt));  // open: gt, eq
  Comparator #(.width(32)) comparator_7 (.a(PrevOldest), .b(counter_7_q), .lt(comparator_7_lt));  // open: gt, eq
  Comparator #(.mode("unsigned"), .width(32)) comparator_8 (
    .a(PrevOldest), .b(counter_8_q), .lt(comparator_8_lt));  // open: gt, eq
  Comparator #(.mode("unsigned"), .width(32)) comparator_9 (
    .a(PrevOldest), .b(counter_9_q), .lt(comparator_9_lt));  // open: gt, eq
  Comparator #(.mode("unsigned"), .width(32)) comparator_10 (
    .a(PrevOldest), .b(counter_10_q), .lt(comparator_10_lt));  // open: gt, eq
  Comparator #(.mode("unsigned"), .width(32)) comparator_11 (
    .a(PrevOldest), .b(counter_11_q), .lt(comparator_11_lt));  // open: gt, eq
  Comparator #(.mode("unsigned"), .width(32)) comparator_12 (
    .a(PrevOldest), .b(counter_12_q), .lt(comparator_12_lt));  // open: gt, eq
  Comparator #(.mode("unsigned"), .width(32)) comparator_13 (
    .a(PrevOldest), .b(counter_13_q), .lt(comparator_13_lt));  // open: gt, eq
  Comparator #(.mode("unsigned"), .width(32)) comparator_14 (
    .a(PrevOldest), .b(counter_14_q), .lt(comparator_14_lt));  // open: gt, eq
  Comparator #(.mode("unsigned"), .width(32)) comparator_15 (
    .a(PrevOldest), .b(counter_15_q), .lt(comparator_15_lt));  // open: gt, eq
  Comparator #(.mode("unsigned"), .width(32)) comparator_16 (
    .a(PrevOldest), .b(counter_16_q), .lt(comparator_16_lt));  // open: gt, eq
  and and_1 (and_1_out, comparator_1_lt, comparator_2_lt);
  and and_2 (and_2_out, comparator_2_lt, comparator_3_lt);
  and and_3 (and_3_out, comparator_3_lt, comparator_4_lt);
  and and_4 (and_4_out, comparator_4_lt, comparator_5_lt);
  and and_5 (and_5_out, comparator_5_lt, comparator_6_lt);
  and and_6 (and_6_out, comparator_6_lt, comparator_7_lt);
  and and_7 (and_7_out, comparator_7_lt, comparator_8_lt);
  and and_8 (and_8_out, comparator_7_lt, comparator_9_lt);
  and and_9 (and_9_out, comparator_9_lt, comparator_10_lt);
  and and_10 (and_10_out, comparator_10_lt, comparator_11_lt);
  and and_11 (and_11_out, comparator_11_lt, comparator_12_lt);
  and and_12 (and_12_out, comparator_12_lt, comparator_13_lt);
  and and_13 (and_13_out, comparator_13_lt, comparator_14_lt);
  and and_14 (and_14_out, comparator_14_lt, comparator_15_lt);
  and and_15 (and_15_out, comparator_15_lt, comparator_16_lt);
  Priority_Encoder #(.select(4)) priority_encoder_1 (
    .in0(comparator_1_lt), .in1(and_1_out), .in2(and_2_out), .in3(and_3_out), .in4(and_4_out),
    .in5(and_5_out), .in6(and_6_out), .in7(and_7_out), .in8(and_8_out), .in9(and_9_out), .in10(and_10_out),
    .in11(and_11_out), .in12(and_12_out), .in13(and_13_out), .in14(and_14_out), .in15(and_15_out),
    .out(OldestAddr));  // open: gs, en_out, en_in
  Pull_Resistor #(.pull(1)) pull_resistor_1 (.node(OldestAddr));
  Multiplexer #(.enable("false"), .select(4), .width(32)) multiplexer_1 (
    .in0(counter_1_q), .in1(counter_2_q), .in2(counter_3_q), .in3(counter_4_q), .in4(counter_5_q),
    .in5(counter_6_q), .in6(counter_7_q), .in7(counter_8_q), .in8(counter_9_q), .in9(counter_10_q),
    .in10(counter_11_q), .in11(counter_12_q), .in12(counter_13_q), .in13(counter_14_q), .in14(counter_15_q),
    .in15(counter_16_q), .out(OldestVal), .sel(OldestAddr));
endmodule

module lru256 (
  input  [31:0] PrevOldest,
  input  Reset,
  input  MemCycle,
  input  [7:0] Addr,
  output [31:0] OldestVal,
  output [7:0] OldestAddr
);

  wire and_1_out, and_2_out, and_3_out, and_4_out, and_5_out, and_6_out, and_7_out, and_8_out, and_9_out,
       and_10_out, and_11_out, and_12_out, and_13_out, and_14_out, and_15_out, comparator_1_lt,
       comparator_2_lt, comparator_3_lt, comparator_4_lt, comparator_5_lt, comparator_6_lt, comparator_7_lt,
       comparator_8_lt, comparator_9_lt, comparator_10_lt, comparator_11_lt, comparator_12_lt,
       comparator_13_lt, comparator_14_lt, comparator_15_lt, comparator_16_lt, demultiplexer_1_out0,
       demultiplexer_1_out1, demultiplexer_1_out2, demultiplexer_1_out3, demultiplexer_1_out4,
       demultiplexer_1_out5, demultiplexer_1_out6, demultiplexer_1_out7, demultiplexer_1_out8,
       demultiplexer_1_out9, demultiplexer_1_out10, demultiplexer_1_out11, demultiplexer_1_out12,
       demultiplexer_1_out13, demultiplexer_1_out14, demultiplexer_1_out15;
  wire [3:0] lru16_1_oldestaddr, lru16_2_oldestaddr, lru16_3_oldestaddr, lru16_4_oldestaddr,
       lru16_5_oldestaddr, lru16_6_oldestaddr, lru16_7_oldestaddr, lru16_8_oldestaddr, lru16_9_oldestaddr,
       lru16_10_oldestaddr, lru16_11_oldestaddr, lru16_12_oldestaddr, lru16_13_oldestaddr,
       lru16_14_oldestaddr, lru16_15_oldestaddr, lru16_16_oldestaddr;
  wire [31:0] lru16_1_oldestval, lru16_2_oldestval, lru16_3_oldestval, lru16_4_oldestval, lru16_5_oldestval,
       lru16_6_oldestval, lru16_7_oldestval, lru16_8_oldestval, lru16_9_oldestval, lru16_10_oldestval,
       lru16_11_oldestval, lru16_12_oldestval, lru16_13_oldestval, lru16_14_oldestval, lru16_15_oldestval,
       lru16_16_oldestval;

  Demultiplexer #(.enable("false"), .select(4)) demultiplexer_1 (
    .out0(demultiplexer_1_out0), .out1(demultiplexer_1_out1), .out2(demultiplexer_1_out2),
    .out3(demultiplexer_1_out3), .out4(demultiplexer_1_out4), .out5(demultiplexer_1_out5),
    .out6(demultiplexer_1_out6), .out7(demultiplexer_1_out7), .out8(demultiplexer_1_out8),
    .out9(demultiplexer_1_out9), .out10(demultiplexer_1_out10), .out11(demultiplexer_1_out11),
    .out12(demultiplexer_1_out12), .out13(demultiplexer_1_out13), .out14(demultiplexer_1_out14),
    .out15(demultiplexer_1_out15), .in(MemCycle), .sel(Addr[7:4]));
  lru16 lru16_1 (
    .OldestVal(lru16_1_oldestval), .OldestAddr(lru16_1_oldestaddr), .Addr(Addr[3:0]),
    .MemCycle(demultiplexer_1_out0), .Reset(Reset), .PrevOldest(PrevOldest));
  lru16 lru16_2 (
    .OldestVal(lru16_2_oldestval), .OldestAddr(lru16_2_oldestaddr), .Addr(Addr[3:0]),
    .MemCycle(demultiplexer_1_out1), .Reset(Reset), .PrevOldest(lru16_1_oldestval));
  lru16 lru16_3 (
    .OldestVal(lru16_3_oldestval), .OldestAddr(lru16_3_oldestaddr), .Addr(Addr[3:0]),
    .MemCycle(demultiplexer_1_out2), .Reset(Reset), .PrevOldest(lru16_2_oldestval));
  lru16 lru16_4 (
    .OldestVal(lru16_4_oldestval), .OldestAddr(lru16_4_oldestaddr), .Addr(Addr[3:0]),
    .MemCycle(demultiplexer_1_out3), .Reset(Reset), .PrevOldest(lru16_3_oldestval));
  lru16 lru16_5 (
    .OldestVal(lru16_5_oldestval), .OldestAddr(lru16_5_oldestaddr), .Addr(Addr[3:0]),
    .MemCycle(demultiplexer_1_out4), .Reset(Reset), .PrevOldest(lru16_4_oldestval));
  lru16 lru16_6 (
    .OldestVal(lru16_6_oldestval), .OldestAddr(lru16_6_oldestaddr), .Addr(Addr[3:0]),
    .MemCycle(demultiplexer_1_out5), .Reset(Reset), .PrevOldest(lru16_5_oldestval));
  lru16 lru16_7 (
    .OldestVal(lru16_7_oldestval), .OldestAddr(lru16_7_oldestaddr), .Addr(Addr[3:0]),
    .MemCycle(demultiplexer_1_out6), .Reset(Reset), .PrevOldest(lru16_6_oldestval));
  lru16 lru16_8 (
    .OldestVal(lru16_8_oldestval), .OldestAddr(lru16_8_oldestaddr), .Addr(Addr[3:0]),
    .MemCycle(demultiplexer_1_out7), .Reset(Reset), .PrevOldest(lru16_7_oldestval));
  lru16 lru16_9 (
    .OldestVal(lru16_9_oldestval), .OldestAddr(lru16_9_oldestaddr), .Addr(Addr[3:0]),
    .MemCycle(demultiplexer_1_out8), .Reset(Reset), .PrevOldest(lru16_8_oldestval));
  lru16 lru16_10 (
    .OldestVal(lru16_10_oldestval), .OldestAddr(lru16_10_oldestaddr), .Addr(Addr[3:0]),
    .MemCycle(demultiplexer_1_out9), .Reset(Reset), .PrevOldest(lru16_9_oldestval));
  lru16 lru16_11 (
    .OldestVal(lru16_11_oldestval), .OldestAddr(lru16_11_oldestaddr), .Addr(Addr[3:0]),
    .MemCycle(demultiplexer_1_out10), .Reset(Reset), .PrevOldest(lru16_10_oldestval));
  lru16 lru16_12 (
    .OldestVal(lru16_12_oldestval), .OldestAddr(lru16_12_oldestaddr), .Addr(Addr[3:0]),
    .MemCycle(demultiplexer_1_out11), .Reset(Reset), .PrevOldest(lru16_11_oldestval));
  lru16 lru16_13 (
    .OldestVal(lru16_13_oldestval), .OldestAddr(lru16_13_oldestaddr), .Addr(Addr[3:0]),
    .MemCycle(demultiplexer_1_out12), .Reset(Reset), .PrevOldest(lru16_12_oldestval));
  lru16 lru16_14 (
    .OldestVal(lru16_14_oldestval), .OldestAddr(lru16_14_oldestaddr), .Addr(Addr[3:0]),
    .MemCycle(demultiplexer_1_out13), .Reset(Reset), .PrevOldest(lru16_13_oldestval));
  lru16 lru16_15 (
    .OldestVal(lru16_15_oldestval), .OldestAddr(lru16_15_oldestaddr), .Addr(Addr[3:0]),
    .MemCycle(demultiplexer_1_out14), .Reset(Reset), .PrevOldest(lru16_14_oldestval));
  lru16 lru16_16 (
    .OldestVal(lru16_16_oldestval), .OldestAddr(lru16_16_oldestaddr), .Addr(Addr[3:0]),
    .MemCycle(demultiplexer_1_out15), .Reset(Reset), .PrevOldest(lru16_15_oldestval));
  Comparator #(.mode("unsigned"), .width(32)) comparator_1 (
    .a(PrevOldest), .b(lru16_1_oldestval), .lt(comparator_1_lt));  // open: gt, eq
  Comparator #(.mode("unsigned"), .width(32)) comparator_2 (
    .a(PrevOldest), .b(lru16_2_oldestval), .lt(comparator_2_lt));  // open: gt, eq
  Comparator #(.mode("unsigned"), .width(32)) comparator_3 (
    .a(PrevOldest), .b(lru16_3_oldestval), .lt(comparator_3_lt));  // open: gt, eq
  Comparator #(.mode("unsigned"), .width(32)) comparator_4 (
    .a(PrevOldest), .b(lru16_4_oldestval), .lt(comparator_4_lt));  // open: gt, eq
  Comparator #(.mode("unsigned"), .width(32)) comparator_5 (
    .a(PrevOldest), .b(lru16_5_oldestval), .lt(comparator_5_lt));  // open: gt, eq
  Comparator #(.mode("unsigned"), .width(32)) comparator_6 (
    .a(PrevOldest), .b(lru16_6_oldestval), .lt(comparator_6_lt));  // open: gt, eq
  Comparator #(.mode("unsigned"), .width(32)) comparator_7 (
    .a(PrevOldest), .b(lru16_7_oldestval), .lt(comparator_7_lt));  // open: gt, eq
  Comparator #(.mode("unsigned"), .width(32)) comparator_8 (
    .a(PrevOldest), .b(lru16_8_oldestval), .lt(comparator_8_lt));  // open: gt, eq
  Comparator #(.mode("unsigned"), .width(32)) comparator_9 (
    .a(PrevOldest), .b(lru16_9_oldestval), .lt(comparator_9_lt));  // open: gt, eq
  Comparator #(.mode("unsigned"), .width(32)) comparator_10 (
    .a(PrevOldest), .b(lru16_10_oldestval), .lt(comparator_10_lt));  // open: gt, eq
  Comparator #(.mode("unsigned"), .width(32)) comparator_11 (
    .a(PrevOldest), .b(lru16_11_oldestval), .lt(comparator_11_lt));  // open: gt, eq
  Comparator #(.mode("unsigned"), .width(32)) comparator_12 (
    .a(PrevOldest), .b(lru16_12_oldestval), .lt(comparator_12_lt));  // open: gt, eq
  Comparator #(.mode("unsigned"), .width(32)) comparator_13 (
    .a(PrevOldest), .b(lru16_13_oldestval), .lt(comparator_13_lt));  // open: gt, eq
  Comparator #(.mode("unsigned"), .width(32)) comparator_14 (
    .a(PrevOldest), .b(lru16_14_oldestval), .lt(comparator_14_lt));  // open: gt, eq
  Comparator #(.mode("unsigned"), .width(32)) comparator_15 (
    .a(PrevOldest), .b(lru16_15_oldestval), .lt(comparator_15_lt));  // open: gt, eq
  Comparator #(.mode("unsigned"), .width(32)) comparator_16 (
    .a(PrevOldest), .b(lru16_16_oldestval), .lt(comparator_16_lt));  // open: gt, eq
  and and_1 (and_1_out, comparator_1_lt, comparator_2_lt);
  and and_2 (and_2_out, comparator_2_lt, comparator_3_lt);
  and and_3 (and_3_out, comparator_3_lt, comparator_4_lt);
  and and_4 (and_4_out, comparator_4_lt, comparator_5_lt);
  and and_5 (and_5_out, comparator_5_lt, comparator_6_lt);
  and and_6 (and_6_out, comparator_6_lt, comparator_7_lt);
  and and_7 (and_7_out, comparator_7_lt, comparator_8_lt);
  and and_8 (and_8_out, comparator_7_lt, comparator_9_lt);
  and and_9 (and_9_out, comparator_9_lt, comparator_10_lt);
  and and_10 (and_10_out, comparator_10_lt, comparator_11_lt);
  and and_11 (and_11_out, comparator_11_lt, comparator_12_lt);
  and and_12 (and_12_out, comparator_12_lt, comparator_13_lt);
  and and_13 (and_13_out, comparator_13_lt, comparator_14_lt);
  and and_14 (and_14_out, comparator_14_lt, comparator_15_lt);
  and and_15 (and_15_out, comparator_15_lt, comparator_16_lt);
  Multiplexer #(.enable("false"), .select(4), .width(32)) multiplexer_1 (
    .in0(lru16_1_oldestval), .in1(lru16_2_oldestval), .in2(lru16_3_oldestval), .in3(lru16_4_oldestval),
    .in4(lru16_5_oldestval), .in5(lru16_6_oldestval), .in6(lru16_7_oldestval), .in7(lru16_8_oldestval),
    .in8(lru16_9_oldestval), .in9(lru16_10_oldestval), .in10(lru16_11_oldestval), .in11(lru16_12_oldestval),
    .in12(lru16_13_oldestval), .in13(lru16_14_oldestval), .in14(lru16_15_oldestval),
    .in15(lru16_16_oldestval), .out(OldestVal), .sel(OldestAddr[7:4]));
  Multiplexer #(.enable("false"), .select(4), .width(4)) multiplexer_2 (
    .in0(lru16_1_oldestaddr), .in1(lru16_2_oldestaddr), .in2(lru16_3_oldestaddr), .in3(lru16_4_oldestaddr),
    .in4(lru16_5_oldestaddr), .in5(lru16_6_oldestaddr), .in6(lru16_7_oldestaddr), .in7(lru16_8_oldestaddr),
    .in8(lru16_9_oldestaddr), .in9(lru16_10_oldestaddr), .in10(lru16_11_oldestaddr),
    .in11(lru16_12_oldestaddr), .in12(lru16_13_oldestaddr), .in13(lru16_14_oldestaddr),
    .in14(lru16_15_oldestaddr), .in15(lru16_16_oldestaddr), .out(OldestAddr[3:0]), .sel(OldestAddr[7:4]));
  Pull_Resistor #(.pull(1)) pull_resistor_1 (.node(OldestAddr[7:4]));
  Priority_Encoder #(.select(4)) priority_encoder_1 (
    .in0(comparator_1_lt), .in1(and_1_out), .in2(and_2_out), .in3(and_3_out), .in4(and_4_out),
    .in5(and_5_out), .in6(and_6_out), .in7(and_7_out), .in8(and_8_out), .in9(and_9_out), .in10(and_10_out),
    .in11(and_11_out), .in12(and_12_out), .in13(and_13_out), .in14(and_14_out), .in15(and_15_out),
    .out(OldestAddr[7:4]));  // open: gs, en_out, en_in
endmodule
module lru4k (
  input  Reset,
  input  MemCycle,
  input  [11:0] Addr,
  output [11:0] OldestAddr
);

  wire and_1_out, and_2_out, and_3_out, and_4_out, and_5_out, and_6_out, and_7_out, and_8_out, and_9_out,
       and_10_out, and_11_out, and_12_out, and_13_out, and_14_out, and_15_out, comparator_1_lt,
       comparator_2_lt, comparator_3_lt, comparator_4_lt, comparator_5_lt, comparator_6_lt, comparator_7_lt,
       comparator_8_lt, comparator_9_lt, comparator_10_lt, comparator_11_lt, comparator_12_lt,
       comparator_13_lt, comparator_14_lt, comparator_15_lt, comparator_16_lt, demultiplexer_1_out0,
       demultiplexer_1_out1, demultiplexer_1_out2, demultiplexer_1_out3, demultiplexer_1_out4,
       demultiplexer_1_out5, demultiplexer_1_out6, demultiplexer_1_out7, demultiplexer_1_out8,
       demultiplexer_1_out9, demultiplexer_1_out10, demultiplexer_1_out11, demultiplexer_1_out12,
       demultiplexer_1_out13, demultiplexer_1_out14, demultiplexer_1_out15;
  wire [7:0] lru256_1_oldestaddr, lru256_2_oldestaddr, lru256_3_oldestaddr, lru256_4_oldestaddr,
       lru256_5_oldestaddr, lru256_6_oldestaddr, lru256_7_oldestaddr, lru256_8_oldestaddr,
       lru256_9_oldestaddr, lru256_10_oldestaddr, lru256_11_oldestaddr, lru256_12_oldestaddr,
       lru256_13_oldestaddr, lru256_14_oldestaddr, lru256_15_oldestaddr, lru256_16_oldestaddr;
  wire [31:0] lru256_1_oldestval, lru256_2_oldestval, lru256_3_oldestval, lru256_4_oldestval,
       lru256_5_oldestval, lru256_6_oldestval, lru256_7_oldestval, lru256_8_oldestval, lru256_9_oldestval,
       lru256_10_oldestval, lru256_11_oldestval, lru256_12_oldestval, lru256_13_oldestval,
       lru256_14_oldestval, lru256_15_oldestval, lru256_16_oldestval;

  Demultiplexer #(.enable("false"), .select(4)) demultiplexer_1 (
    .out0(demultiplexer_1_out0), .out1(demultiplexer_1_out1), .out2(demultiplexer_1_out2),
    .out3(demultiplexer_1_out3), .out4(demultiplexer_1_out4), .out5(demultiplexer_1_out5),
    .out6(demultiplexer_1_out6), .out7(demultiplexer_1_out7), .out8(demultiplexer_1_out8),
    .out9(demultiplexer_1_out9), .out10(demultiplexer_1_out10), .out11(demultiplexer_1_out11),
    .out12(demultiplexer_1_out12), .out13(demultiplexer_1_out13), .out14(demultiplexer_1_out14),
    .out15(demultiplexer_1_out15), .in(MemCycle), .sel(Addr[11:8]));
  lru256 lru256_1 (
    .OldestVal(lru256_1_oldestval), .OldestAddr(lru256_1_oldestaddr), .Addr(Addr[7:0]), .PrevOldest(32'h1),
    .MemCycle(demultiplexer_1_out0), .Reset(Reset));
  lru256 lru256_2 (
    .OldestVal(lru256_2_oldestval), .OldestAddr(lru256_2_oldestaddr), .Addr(Addr[7:0]),
    .PrevOldest(lru256_1_oldestval), .MemCycle(demultiplexer_1_out1), .Reset(Reset));
  lru256 lru256_3 (
    .OldestVal(lru256_3_oldestval), .OldestAddr(lru256_3_oldestaddr), .Addr(Addr[7:0]),
    .PrevOldest(lru256_2_oldestval), .MemCycle(demultiplexer_1_out2), .Reset(Reset));
  lru256 lru256_4 (
    .OldestVal(lru256_4_oldestval), .OldestAddr(lru256_4_oldestaddr), .Addr(Addr[7:0]),
    .PrevOldest(lru256_3_oldestval), .MemCycle(demultiplexer_1_out3), .Reset(Reset));
  lru256 lru256_5 (
    .OldestVal(lru256_5_oldestval), .OldestAddr(lru256_5_oldestaddr), .Addr(Addr[7:0]),
    .PrevOldest(lru256_4_oldestval), .MemCycle(demultiplexer_1_out4), .Reset(Reset));
  lru256 lru256_6 (
    .OldestVal(lru256_6_oldestval), .OldestAddr(lru256_6_oldestaddr), .Addr(Addr[7:0]),
    .PrevOldest(lru256_5_oldestval), .MemCycle(demultiplexer_1_out5), .Reset(Reset));
  lru256 lru256_7 (
    .OldestVal(lru256_7_oldestval), .OldestAddr(lru256_7_oldestaddr), .Addr(Addr[7:0]),
    .PrevOldest(lru256_6_oldestval), .MemCycle(demultiplexer_1_out6), .Reset(Reset));
  lru256 lru256_8 (
    .OldestVal(lru256_8_oldestval), .OldestAddr(lru256_8_oldestaddr), .Addr(Addr[7:0]),
    .PrevOldest(lru256_7_oldestval), .MemCycle(demultiplexer_1_out7), .Reset(Reset));
  lru256 lru256_9 (
    .OldestVal(lru256_9_oldestval), .OldestAddr(lru256_9_oldestaddr), .Addr(Addr[7:0]),
    .PrevOldest(lru256_8_oldestval), .MemCycle(demultiplexer_1_out8), .Reset(Reset));
  lru256 lru256_10 (
    .OldestVal(lru256_10_oldestval), .OldestAddr(lru256_10_oldestaddr), .Addr(Addr[7:0]),
    .PrevOldest(lru256_9_oldestval), .MemCycle(demultiplexer_1_out9), .Reset(Reset));
  lru256 lru256_11 (
    .OldestVal(lru256_11_oldestval), .OldestAddr(lru256_11_oldestaddr), .Addr(Addr[7:0]),
    .PrevOldest(lru256_10_oldestval), .MemCycle(demultiplexer_1_out10), .Reset(Reset));
  lru256 lru256_12 (
    .OldestVal(lru256_12_oldestval), .OldestAddr(lru256_12_oldestaddr), .Addr(Addr[7:0]),
    .PrevOldest(lru256_11_oldestval), .MemCycle(demultiplexer_1_out11), .Reset(Reset));
  lru256 lru256_13 (
    .OldestVal(lru256_13_oldestval), .OldestAddr(lru256_13_oldestaddr), .Addr(Addr[7:0]),
    .PrevOldest(lru256_12_oldestval), .MemCycle(demultiplexer_1_out12), .Reset(Reset));
  lru256 lru256_14 (
    .OldestVal(lru256_14_oldestval), .OldestAddr(lru256_14_oldestaddr), .Addr(Addr[7:0]),
    .PrevOldest(lru256_13_oldestval), .MemCycle(demultiplexer_1_out13), .Reset(Reset));
  lru256 lru256_15 (
    .OldestVal(lru256_15_oldestval), .OldestAddr(lru256_15_oldestaddr), .Addr(Addr[7:0]),
    .PrevOldest(lru256_14_oldestval), .MemCycle(demultiplexer_1_out14), .Reset(Reset));
  lru256 lru256_16 (
    .OldestVal(lru256_16_oldestval), .OldestAddr(lru256_16_oldestaddr), .Addr(Addr[7:0]),
    .PrevOldest(lru256_15_oldestval), .MemCycle(demultiplexer_1_out15), .Reset(Reset));
  Comparator #(.mode("unsigned"), .width(32)) comparator_1 (
    .a(32'h1), .b(lru256_1_oldestval), .lt(comparator_1_lt));  // open: gt, eq
  Comparator #(.mode("unsigned"), .width(32)) comparator_2 (
    .a(32'h1), .b(lru256_2_oldestval), .lt(comparator_2_lt));  // open: gt, eq
  Comparator #(.mode("unsigned"), .width(32)) comparator_3 (
    .a(32'h1), .b(lru256_3_oldestval), .lt(comparator_3_lt));  // open: gt, eq
  Comparator #(.mode("unsigned"), .width(32)) comparator_4 (
    .a(32'h1), .b(lru256_4_oldestval), .lt(comparator_4_lt));  // open: gt, eq
  Comparator #(.mode("unsigned"), .width(32)) comparator_5 (
    .a(32'h1), .b(lru256_5_oldestval), .lt(comparator_5_lt));  // open: gt, eq
  Comparator #(.mode("unsigned"), .width(32)) comparator_6 (
    .a(32'h1), .b(lru256_6_oldestval), .lt(comparator_6_lt));  // open: gt, eq
  Comparator #(.mode("unsigned"), .width(32)) comparator_7 (
    .a(32'h1), .b(lru256_7_oldestval), .lt(comparator_7_lt));  // open: gt, eq
  Comparator #(.mode("unsigned"), .width(32)) comparator_8 (
    .a(32'h1), .b(lru256_8_oldestval), .lt(comparator_8_lt));  // open: gt, eq
  Comparator #(.mode("unsigned"), .width(32)) comparator_9 (
    .a(32'h1), .b(lru256_9_oldestval), .lt(comparator_9_lt));  // open: gt, eq
  Comparator #(.mode("unsigned"), .width(32)) comparator_10 (
    .a(32'h1), .b(lru256_10_oldestval), .lt(comparator_10_lt));  // open: gt, eq
  Comparator #(.mode("unsigned"), .width(32)) comparator_11 (
    .a(32'h1), .b(lru256_11_oldestval), .lt(comparator_11_lt));  // open: gt, eq
  Comparator #(.mode("unsigned"), .width(32)) comparator_12 (
    .a(32'h1), .b(lru256_12_oldestval), .lt(comparator_12_lt));  // open: gt, eq
  Comparator #(.mode("unsigned"), .width(32)) comparator_13 (
    .a(32'h1), .b(lru256_13_oldestval), .lt(comparator_13_lt));  // open: gt, eq
  Comparator #(.mode("unsigned"), .width(32)) comparator_14 (
    .a(32'h1), .b(lru256_14_oldestval), .lt(comparator_14_lt));  // open: gt, eq
  Comparator #(.mode("unsigned"), .width(32)) comparator_15 (
    .a(32'h1), .b(lru256_15_oldestval), .lt(comparator_15_lt));  // open: gt, eq
  Comparator #(.mode("unsigned"), .width(32)) comparator_16 (
    .a(32'h1), .b(lru256_16_oldestval), .lt(comparator_16_lt));  // open: gt, eq
  and and_1 (and_1_out, comparator_1_lt, comparator_2_lt);
  and and_2 (and_2_out, comparator_2_lt, comparator_3_lt);
  and and_3 (and_3_out, comparator_3_lt, comparator_4_lt);
  and and_4 (and_4_out, comparator_4_lt, comparator_5_lt);
  and and_5 (and_5_out, comparator_5_lt, comparator_6_lt);
  and and_6 (and_6_out, comparator_6_lt, comparator_7_lt);
  and and_7 (and_7_out, comparator_7_lt, comparator_8_lt);
  and and_8 (and_8_out, comparator_7_lt, comparator_9_lt);
  and and_9 (and_9_out, comparator_9_lt, comparator_10_lt);
  and and_10 (and_10_out, comparator_10_lt, comparator_11_lt);
  and and_11 (and_11_out, comparator_11_lt, comparator_12_lt);
  and and_12 (and_12_out, comparator_12_lt, comparator_13_lt);
  and and_13 (and_13_out, comparator_13_lt, comparator_14_lt);
  and and_14 (and_14_out, comparator_14_lt, comparator_15_lt);
  and and_15 (and_15_out, comparator_15_lt, comparator_16_lt);
  Multiplexer #(.enable("false"), .select(4), .width(8)) multiplexer_1 (
    .in0(lru256_1_oldestaddr), .in1(lru256_2_oldestaddr), .in2(lru256_3_oldestaddr),
    .in3(lru256_4_oldestaddr), .in4(lru256_5_oldestaddr), .in5(lru256_6_oldestaddr),
    .in6(lru256_7_oldestaddr), .in7(lru256_8_oldestaddr), .in8(lru256_9_oldestaddr),
    .in9(lru256_10_oldestaddr), .in10(lru256_11_oldestaddr), .in11(lru256_12_oldestaddr),
    .in12(lru256_13_oldestaddr), .in13(lru256_14_oldestaddr), .in14(lru256_15_oldestaddr),
    .in15(lru256_16_oldestaddr), .out(OldestAddr[7:0]), .sel(OldestAddr[11:8]));
  Priority_Encoder #(.select(4)) priority_encoder_1 (
    .in0(comparator_1_lt), .in1(and_1_out), .in2(and_2_out), .in3(and_3_out), .in4(and_4_out),
    .in5(and_5_out), .in6(and_6_out), .in7(and_7_out), .in8(and_8_out), .in9(and_9_out), .in10(and_10_out),
    .in11(and_11_out), .in12(and_12_out), .in13(and_13_out), .in14(and_14_out), .in15(and_15_out),
    .out(OldestAddr[11:8]));  // open: gs, en_out, en_in
  Pull_Resistor #(.pull(1)) pull_resistor_1 (.node(OldestAddr[11:8]));
endmodule

module pgfetcher (
  input  MemCycle,
  input  TLBHit,
  input  Reset,
  input  Clock,
  input  [51:0] PgNoIn,
  input  [63:0] Din,
  input  [63:0] PL6P_Data,
  input  PL6P_Wr,
  output [63:0] WalkAddress,
  output TLBWr,
  output PGStructWalk,
  output [63:0] FetchedEntry
);

  wire comparator_1_eq, decoder_1_out0, decoder_1_out1, decoder_1_out2, decoder_1_out3, decoder_1_out4,
       decoder_1_out5, decoder_1_out6, or_1_out, or_2_out, PGStructWalk_t;
  wire [2:0] FetchPhase;
  wire [8:0] bit_extender_1_out;
  wire [63:0] register_2_q;

  or or_1 (or_1_out, Reset, TLBHit);
  Counter #(.max('h7), .width(3)) counter_1 (
    .count(PGStructWalk_t), .Q(FetchPhase), .clk(Clock), .clr(or_1_out));  // open: load, D, carry, up
  D_Flip_Flop d_ff_1 (.clk(Clock), .D(MemCycle), .Q(PGStructWalk_t), .reset(or_2_out));  // open: Qn, preset
  assign bit_extender_1_out = {{2{1'b0}}, PgNoIn[51:45]};  // Bit_Extender bit_extender_1
  or or_2 (or_2_out, TLBHit, Reset);
  Multiplexer #(.enable("false"), .select(3), .width(9)) multiplexer_1 (
    .in0(bit_extender_1_out), .in1(PgNoIn[44:36]), .in2(PgNoIn[35:27]), .in3(PgNoIn[26:18]),
    .in4(PgNoIn[17:9]), .in5(PgNoIn[8:0]), .out(WalkAddress[11:3]), .sel(FetchPhase));  // open: in6, in7
  Register #(.width(64)) register_1 (.D(Din), .en(PGStructWalk_t), .Q(FetchedEntry), .clk(Clock), .clr(Reset));
  Register #(.width(64)) register_2 (.D(PL6P_Data), .en(PL6P_Wr), .Q(register_2_q), .clk(Clock));  // open: clr
  Comparator #(.mode("unsigned"), .width(3)) comparator_1 (
    .a(FetchPhase), .b(3'b000), .eq(comparator_1_eq));  // open: gt, lt
  Comparator #(.mode("unsigned"), .width(3)) comparator_2 (.a(FetchPhase), .b(3'b110), .eq(TLBWr));  // open: gt, lt
  Multiplexer #(.enable("false"), .width(52)) multiplexer_2 (
    .in0(FetchedEntry[63:12]), .in1(register_2_q[63:12]), .out(WalkAddress[63:12]), .sel(comparator_1_eq));
  Decoder #(.select(3)) decoder_1 (
    .out0(decoder_1_out0), .out1(decoder_1_out1), .out2(decoder_1_out2), .out3(decoder_1_out3),
    .out4(decoder_1_out4), .out5(decoder_1_out5), .out6(decoder_1_out6), .en(PGStructWalk_t));  // open: out7, sel
  or or_3 (PGStructWalk, ~TLBHit, PGStructWalk_t);  // OR_Gate
  // Buzzer buzzer_1: pin names not known; wires that end beside it: 14'h188, decoder_1_out0
  // Buzzer buzzer_2: pin names not known; wires that end beside it: 14'h1b8, decoder_1_out1
  // Buzzer buzzer_3: pin names not known; wires that end beside it: 14'h1ee, decoder_1_out2
  // Buzzer buzzer_4: pin names not known; wires that end beside it: 14'h24b, decoder_1_out3
  // Buzzer buzzer_5: pin names not known; wires that end beside it: 14'h293, decoder_1_out4
  // Buzzer buzzer_6: pin names not known; wires that end beside it: 14'h2ba, decoder_1_out5
  // Buzzer buzzer_7: pin names not known; wires that end beside it: 14'h310, decoder_1_out6

  assign WalkAddress[2:0] = 3'b000;

  // Other names for the same wires on the sheet: PGOffset[8:0] = WalkAddress[11:3]
endmodule
